// Logisim project Proj2starterMiah.circ as structural Verilog: 5 circuits, main circuit regfile
module CPUmain (
);

  regfile regfile_1 ();  // open: rt, rd, rd_data, write_e, rs, rs_data, rt_data
  Control control_1 ();  // open: Inst, rs, rt, rd, imm, reg_write_e, imm_sel, ALU_code, out_9
  ALU alu_1 ();  // open: OP1, OP2, ALU_CODE, Res
endmodule

module regfile (
  input  [4:0] rs,
  input  [4:0] rt,
  input  [4:0] rd,
  input  write_e,
  input  [31:0] rd_data,
  output [31:0] rs_data,
  output [31:0] rt_data
);
endmodule

module ALU (
  input  [3:0] ALU_CODE,
  input  [31:0] OP1,
  input  [31:0] OP2,
  output Res
);

  Adder adder_1 ();  // open: a, b, out, cin, cout
  Subtractor subtractor_1 ();  // open: a, b, out, bin, bout
  Multiplier multiplier_1 ();  // open: a, b, out, cin, cout
  Divider divider_1 ();  // open: a, b, out, upper, rem
  Register HI ();  // open: D, en, clk, Q, clr
  Register LO ();  // open: D, en, clk, Q, clr
endmodule

module Control (
  input  [31:0] Inst,
  output [4:0] rs,
  output [4:0] rt,
  output [4:0] rd,
  output [31:0] imm,
  output reg_write_e,
  output imm_sel,
  output [3:0] ALU_code,
  output out_9
);

  wire comparator_1_eq, comparator_2_eq, comparator_3_eq, comparator_4_eq, comparator_5_eq, comparator_6_eq,
       comparator_7_eq, comparator_8_eq, comparator_9_eq, undriven_2, undriven_3;
  wire [5:0] undriven;
  wire [6:0] bit_extender_1_out;

  Comparator #(.mode("unsigned"), .width(6)) comparator_1 (.a({6{1'b0}}), .eq(comparator_1_eq));  // open: b, gt, lt
  Comparator #(.mode("unsigned"), .width(6)) comparator_2 (.a(6'b001000), .eq(comparator_2_eq));  // open: b, gt, lt
  Comparator #(.mode("unsigned"), .width(6)) comparator_3 (
    .a(undriven), .b(6'b100100), .eq(comparator_3_eq));  // open: gt, lt
  Comparator #(.mode("unsigned"), .width(6)) comparator_4 (
    .a(undriven), .b(6'b011000), .eq(comparator_4_eq));  // open: gt, lt
  Comparator #(.mode("unsigned"), .width(6)) comparator_5 (
    .a(undriven), .b({6{1'b0}}), .eq(comparator_5_eq));  // open: gt, lt
  assign bit_extender_1_out = {{1{undriven[5]}}, undriven};  // Bit_Extender bit_extender_1
  Comparator #(.mode("unsigned"), .width(7)) comparator_6 (
    .a(bit_extender_1_out), .b(7'b1000010), .eq(comparator_6_eq));  // open: gt, lt
  Comparator #(.mode("unsigned"), .width(6)) comparator_7 (
    .a(undriven), .b(6'b100110), .eq(comparator_7_eq));  // open: gt, lt
  Comparator #(.mode("unsigned"), .width(6)) comparator_8 (
    .a(undriven), .b(6'b010110), .eq(comparator_8_eq));  // open: gt, lt
  Comparator #(.mode("unsigned"), .width(6)) comparator_9 (
    .a(undriven), .b(6'b000010), .eq(comparator_9_eq));  // open: gt, lt
  sixBitDemultiplexor sixbitdemultiplexor_1 (.data(Inst));  // open: add, sub, addi, mult, div, mflo, mfhi, shiftll, shiftrl, slt
  Multiplexer #(.select(4)) multiplexer_1 (
    .in0(undriven_3), .in1(undriven_2), .in2(comparator_3_eq), .in3(comparator_7_eq), .in4(comparator_4_eq),
    .in5(comparator_8_eq), .in6(comparator_5_eq), .in7(comparator_9_eq), .in8(comparator_6_eq), .out(out_9),
    .sel(4'b0110));  // open: in9, in10, in11, in12, in13, in14, in15
  Multiplexer multiplexer_2 ();  // open: in0, in1, out, sel

  // Notes on the sheet:
  //   funct code
  //   slt
  //   add
  //   mult
  //   mflo
  //   sll
  //   sub
  //   div
  //   mfhi
  //   srl
endmodule

module sixBitDemultiplexor (
  input  [31:0] data,
  output [31:0] add,
  output [31:0] sub,
  output [31:0] addi,
  output [31:0] mult,
  output [31:0] div,
  output [31:0] mflo,
  output [31:0] mfhi,
  output [31:0] shiftll,
  output [31:0] shiftrl,
  output [31:0] slt
);

  wire demultiplexer_3_out0, demultiplexer_4_out0, demultiplexer_4_out1, opcode000000_out;

  Demultiplexer #(.select(3)) demultiplexer_1 (
    .in(opcode000000_out), .sel(data[2:0]));  // open: out0, out1, out2, out3, out4, out5, out6, out7
  Demultiplexer #(.select(3)) demultiplexer_2 (
    .in(opcode000000_out), .sel(data[5:3]));  // open: out0, out1, out2, out3, out4, out5, out6, out7
  Demultiplexer #(.select(3)) demultiplexer_3 (
    .out0(demultiplexer_3_out0), .in(1'b1), .sel(data[28:26]));  // open: out1, out2, out3, out4, out5, out6, out7
  Demultiplexer #(.select(3)) demultiplexer_4 (
    .out0(demultiplexer_4_out0), .out1(demultiplexer_4_out1), .in(1'b1), .sel(data[31:29]));  // open: out2, out3, out4, out5, out6, out7
  and opcode000000 (opcode000000_out, demultiplexer_3_out0, demultiplexer_4_out0);
  // AND_Gate opcode001000 has open pins: in0=demultiplexer_4_out1, in1=demultiplexer_3_out0, out=open

  // Notes on the sheet:
  //   order of demultiplexors
  //   funct code
  //   opcode
  //   000
  //   001
  //   010
  //   011
  //   100
  //   101
  //   110
  //   111
  //   lower order bits
  //   higher order bits
  //   lower order bits
  //   higher order bits
  //   need multiplexor to give which funct code is matching the funct code given
endmodule
