// Logisim project MAINProj2starter.circ as structural Verilog: 4 circuits, main circuit regfile
module regfile (
  input  [4:0] rs,
  input  [4:0] rt,
  input  [4:0] rd,
  input  write_e,
  input  [31:0] rd_data,
  output [31:0] rs_data,
  output [31:0] rt_data
);
endmodule

module CPUmain (
);

  wire control_1_imm_sel, multiplexer_1_out, regfile_1_p1, regfile_1_p2, regfile_1_p6, regfile_1_p7;
  wire [3:0] control_1_alu_code;
  wire [4:0] regfile_1_p3, regfile_1_p4, regfile_1_p5;
  wire [31:0] control_1_imm;

  // regfile regfile_1: pin names not known; wires that end beside it: regfile_1_p1, regfile_1_p2, regfile_1_p3, regfile_1_p4, regfile_1_p5, regfile_1_p6, regfile_1_p7
  Control control_1 (
    .Inst({32{1'b0}}), .rs(regfile_1_p4), .rt(regfile_1_p5), .rd(regfile_1_p3), .imm(control_1_imm),
    .reg_write_e(regfile_1_p2), .imm_sel(control_1_imm_sel), .ALU_code(control_1_alu_code));
  Multiplexer multiplexer_1 (
    .in0(regfile_1_p7), .in1(control_1_imm[0]), .out(multiplexer_1_out), .sel(control_1_imm_sel));
  // ALU alu_1: pin names not known; wires that end beside it: regfile_1_p6, multiplexer_1_out, control_1_alu_code, regfile_1_p1
  regfile regfile_2 ();  // open: rt, rd, rd_data, write_e, rs, rs_data, rt_data
  Control control_2 ();  // open: Inst, rs, rt, rd, imm, reg_write_e, imm_sel, ALU_code
  ALU alu_2 ();  // open: OP1, OP2, ALU_CODE, Res
  // Pins of 1 and 32 bits meet at control_1_imm
endmodule

module ALU (
  input  [3:0] ALU_CODE,
  input  [31:0] OP1,
  input  [31:0] OP2,
  output Res
);

  Adder adder_1 ();  // open: a, b, out, cin, cout
  Subtractor subtractor_1 ();  // open: a, b, out, bin, bout
  Multiplier multiplier_1 ();  // open: a, b, out, cin, cout
  Divider divider_1 ();  // open: a, b, out, upper, rem
  Register HI ();  // open: D, en, clk, Q, clr
  Register LO ();  // open: D, en, clk, Q, clr
endmodule

module Control (
  input  [31:0] Inst,
  output [4:0] rs,
  output [4:0] rt,
  output [4:0] rd,
  output [31:0] imm,
  output reg_write_e,
  output imm_sel,
  output [3:0] ALU_code
);
endmodule
