// Logisim project Proj2ALU_Changes.circ as structural Verilog: 1 circuit, main circuit ALU
module ALU (
  input  [31:0] OP1,
  input  [31:0] OP2,
  input  [4:0] ALU_CODE,
  output [31:0] Res
);

  wire comparator_1_lt, comparator_2_eq, comparator_3_eq, or_2_out;
  wire [4:0] bit_extender_1_out, bit_extender_2_out;
  wire [31:0] adder_1_out, and_1_out, bit_extender_3_out, divider_1_out, divider_1_rem, HI_q, LO_q,
       multiplexer_1_out, multiplexer_2_out, multiplier_1_cout, multiplier_1_out, nor_1_out, or_1_out,
       shifter_1_out, shifter_2_out, subtractor_1_out, undriven, undriven_2, undriven_3, undriven_4,
       undriven_5, undriven_6, undriven_7, undriven_8, undriven_9, undriven_10, xor_1_out;

  Bit_Extender #(.in_width(32), .out_width(5)) bit_extender_1 (.in(OP2), .out(bit_extender_1_out));
  Bit_Extender #(.in_width(32), .out_width(5)) bit_extender_2 (.in(OP2), .out(bit_extender_2_out));
  assign or_1_out = OP1 | OP2;  // OR_Gate or_1, 32 bits wide
  assign nor_1_out = ~(OP1 | OP2);  // NOR_Gate nor_1, 32 bits wide
  assign xor_1_out = OP1 ^ OP2;  // XOR_Gate xor_1, 32 bits wide
  assign and_1_out = OP2 & OP1;  // AND_Gate and_1, 32 bits wide
  Comparator #(.mode("unsigned"), .width(32)) comparator_1 (.a(OP1), .b(OP2), .lt(comparator_1_lt));  // open: gt, eq
  Adder #(.width(32)) adder_1 (.a(OP1), .b(OP2), .out(adder_1_out));  // open: cin, cout
  Subtractor #(.width(32)) subtractor_1 (.a(OP1), .b(OP2), .out(subtractor_1_out));  // open: bin, bout
  Multiplier #(.width(32)) multiplier_1 (
    .a(OP1), .b(OP2), .out(multiplier_1_out), .cout(multiplier_1_cout));  // open: cin
  Divider #(.width(32)) divider_1 (.a(OP2), .b(OP1), .out(divider_1_out), .rem(divider_1_rem));  // open: upper
  Shifter #(.width(32)) shifter_1 (.in(OP1), .\dist (bit_extender_1_out), .out(shifter_1_out));
  Shifter #(.shift("lr"), .width(32)) shifter_2 (.in(OP1), .\dist (bit_extender_2_out), .out(shifter_2_out));
  assign bit_extender_3_out = {{31{comparator_1_lt}}, comparator_1_lt};  // Bit_Extender bit_extender_3
  Multiplexer #(.width(32)) multiplexer_1 (
    .in0(multiplier_1_cout), .in1(divider_1_rem), .out(multiplexer_1_out), .sel(comparator_3_eq));
  Comparator #(.width(5)) comparator_2 (.a(ALU_CODE), .b(5'b00011), .eq(comparator_2_eq));  // open: gt, lt
  Comparator #(.width(5)) comparator_3 (.a(ALU_CODE), .b(5'b00100), .eq(comparator_3_eq));  // open: gt, lt
  Multiplexer #(.width(32)) multiplexer_2 (
    .in0(multiplier_1_out), .in1(divider_1_out), .out(multiplexer_2_out), .sel(comparator_3_eq));
  Multiplexer #(.select(5), .width(32)) multiplexer_3 (
    .in0(adder_1_out), .in1(subtractor_1_out), .in2(multiplier_1_out), .in3(divider_1_out), .in4(LO_q),
    .in5(HI_q), .in6(shifter_1_out), .in7(shifter_2_out), .in8(or_1_out), .in9(undriven), .in10(xor_1_out),
    .in11(and_1_out), .in12(bit_extender_3_out), .in13(undriven_2), .in14(undriven_3), .in15(undriven_4),
    .in16(undriven_5), .in17(undriven_6), .in18(undriven_7), .in19(undriven_8), .in20(undriven_9),
    .in21(undriven_10), .out(Res), .sel(ALU_CODE));  // open: in22, in23, in24, in25, in26, in27, in28, in29, in30, in31
  or or_2 (or_2_out, comparator_2_eq, comparator_3_eq);
  Register #(.width(32)) HI (.D(multiplexer_1_out), .en(or_2_out), .Q(HI_q));  // open: clk, clr
  Register #(.width(32)) LO (.D(multiplexer_2_out), .en(or_2_out), .Q(LO_q));  // open: clk, clr

  // Notes on the sheet:
  //   OP1
  //   OP2
  //   j
  //   jal
  //   jr
  //   jalr
  //   syscall
  //   lw
  //   sw
  //   beq
  //   bne
  //   hi
endmodule
