// Logisim project Proj2starter.circ as structural Verilog: 5 circuits, main circuit regfile
module CPUmain (
);

  regfile regfile_1 ();  // open: rt, rd, rd_data, write_e, rs, rs_data, rt_data
  Control control_1 ();  // open: Inst, rs, rt, rd, imm, reg_write_e, imm_sel, ALU_code
  ALU alu_1 ();  // open: OP1, OP2, ALU_CODE, Res
endmodule

module regfile (
  input  [4:0] rs,
  input  [4:0] rt,
  input  [4:0] rd,
  input  write_e,
  input  [31:0] rd_data,
  output [31:0] rs_data,
  output [31:0] rt_data
);
endmodule

module ALU (
  input  [3:0] ALU_CODE,
  input  [31:0] OP1,
  input  [31:0] OP2,
  output Res
);

  Adder adder_1 ();  // open: a, b, out, cin, cout
  Subtractor subtractor_1 ();  // open: a, b, out, bin, bout
  Multiplier multiplier_1 ();  // open: a, b, out, cin, cout
  Divider divider_1 ();  // open: a, b, out, upper, rem
  Register HI ();  // open: D, en, clk, Q, clr
  Register LO ();  // open: D, en, clk, Q, clr
endmodule

module Control (
  input  [31:0] Inst,
  output [4:0] rs,
  output [4:0] rt,
  output [4:0] rd,
  output [31:0] imm,
  output reg_write_e,
  output imm_sel,
  output [3:0] ALU_code
);
endmodule

module TESTminiRegFile (
  input  [4:0] rs,
  input  [4:0] rt,
  input  [4:0] rd,
  input  WE,
  input  [31:0] rdData,
  output [31:0] rsData
);

  wire [31:0] reg1_q, reg2_q, reg3_q, reg4_q;

  Register #(.width(32)) reg1 (.Q(reg1_q));  // open: D, en, clk, clr
  Register #(.width(32)) reg2 (.Q(reg2_q));  // open: D, en, clk, clr
  Register #(.width(32)) reg3 (.Q(reg3_q));  // open: D, en, clk, clr
  Register #(.width(32)) reg4 (.Q(reg4_q));  // open: D, en, clk, clr
  Multiplexer #(.select(5), .width(32)) multiplexer_1 (
    .in0({32{1'b0}}), .in1(reg1_q), .in2(reg2_q), .in3(reg3_q), .in4(reg4_q), .sel(rs));  // open: in5, in6, in7, in8, in9, in10, in11, in12, in13, in14, in15, in16, in17, in18, in19, in20, in21, in22, in23, in24, in25, in26, in27, in28, in29, in30, in31, out
endmodule
