// Logisim project ProjectMain.circ as structural Verilog: 22 circuits, main circuit regfile
module CPUmain (
);

  wire control_1_imm_sel, control_1_reg_write_e;
  wire [4:0] control_1_alu_code, control_1_rd, control_1_rs, control_1_rt;
  wire [31:0] alu_1_res, control_1_imm, multiplexer_1_out, regfile_1_rs_data, regfile_1_rt_data;

  regfile regfile_1 (
    .rd_data(alu_1_res), .rd(control_1_rs), .write_e(control_1_reg_write_e), .rt(control_1_rt),
    .rs(control_1_rd), .rs_data(regfile_1_rs_data), .rt_data(regfile_1_rt_data));
  Control control_1 (
    .Inst({32{1'b0}}), .rd(control_1_rd), .rt(control_1_rt), .rs(control_1_rs), .imm(control_1_imm),
    .reg_write_e(control_1_reg_write_e), .imm_sel(control_1_imm_sel), .ALU_code(control_1_alu_code));
  Multiplexer #(.width(32)) multiplexer_1 (
    .in0(regfile_1_rt_data), .in1(control_1_imm), .out(multiplexer_1_out), .sel(control_1_imm_sel));
  ALU alu_1 (.ALU_CODE(control_1_alu_code), .OP1(regfile_1_rs_data), .OP2(multiplexer_1_out), .Res(alu_1_res));
endmodule

module ALU (
  input  [31:0] OP1,
  input  [31:0] OP2,
  input  [4:0] ALU_CODE,
  output [31:0] Res
);

  wire comparator_1_lt, comparator_2_eq, comparator_3_eq, or_2_out;
  wire [4:0] bit_extender_1_out, bit_extender_2_out;
  wire [31:0] adder_1_out, and_1_out, bit_extender_3_out, divider_1_out, divider_1_rem, HI_q, LO_q,
       multiplexer_1_out, multiplexer_2_out, multiplier_1_cout, multiplier_1_out, nor_1_out, or_1_out,
       shifter_1_out, shifter_2_out, subtractor_1_out, undriven, xor_1_out;

  Bit_Extender #(.in_width(32), .out_width(5)) bit_extender_1 (.in(OP2), .out(bit_extender_1_out));
  Bit_Extender #(.in_width(32), .out_width(5)) bit_extender_2 (.in(OP2), .out(bit_extender_2_out));
  assign or_1_out = OP1 | OP2;  // OR_Gate or_1, 32 bits wide
  assign nor_1_out = ~(OP1 | OP2);  // NOR_Gate nor_1, 32 bits wide
  assign xor_1_out = OP1 ^ OP2;  // XOR_Gate xor_1, 32 bits wide
  assign and_1_out = OP2 & OP1;  // AND_Gate and_1, 32 bits wide
  Comparator #(.mode("unsigned"), .width(32)) comparator_1 (.a(OP1), .b(OP2), .lt(comparator_1_lt));  // open: gt, eq
  Adder #(.width(32)) adder_1 (.a(OP1), .b(OP2), .out(adder_1_out));  // open: cin, cout
  Subtractor #(.width(32)) subtractor_1 (.a(OP1), .b(OP2), .out(subtractor_1_out));  // open: bin, bout
  Multiplier #(.width(32)) multiplier_1 (
    .a(OP1), .b(OP2), .out(multiplier_1_out), .cout(multiplier_1_cout));  // open: cin
  Divider #(.width(32)) divider_1 (.a(OP2), .b(OP1), .out(divider_1_out), .rem(divider_1_rem));  // open: upper
  Shifter #(.width(32)) shifter_1 (.in(OP1), .\dist (bit_extender_1_out), .out(shifter_1_out));
  Shifter #(.shift("lr"), .width(32)) shifter_2 (.in(OP1), .\dist (bit_extender_2_out), .out(shifter_2_out));
  assign bit_extender_3_out = {{31{comparator_1_lt}}, comparator_1_lt};  // Bit_Extender bit_extender_3
  Multiplexer #(.width(32)) multiplexer_1 (
    .in0(multiplier_1_cout), .in1(divider_1_rem), .out(multiplexer_1_out), .sel(comparator_3_eq));
  Comparator #(.width(5)) comparator_2 (.a(ALU_CODE), .b(5'b00011), .eq(comparator_2_eq));  // open: gt, lt
  Comparator #(.width(5)) comparator_3 (.a(ALU_CODE), .b(5'b00100), .eq(comparator_3_eq));  // open: gt, lt
  Multiplexer #(.width(32)) multiplexer_2 (
    .in0(multiplier_1_out), .in1(divider_1_out), .out(multiplexer_2_out), .sel(comparator_3_eq));
  Multiplexer #(.select(5), .width(32)) multiplexer_3 (
    .in0(adder_1_out), .in1(subtractor_1_out), .in2(multiplier_1_out), .in3(divider_1_out), .in4(LO_q),
    .in5(HI_q), .in6(shifter_1_out), .in7(shifter_2_out), .in8(or_1_out), .in9(undriven), .in10(xor_1_out),
    .in11(and_1_out), .in12(bit_extender_3_out), .out(Res), .sel(ALU_CODE));  // open: in13, in14, in15, in16, in17, in18, in19, in20, in21, in22, in23, in24, in25, in26, in27, in28, in29, in30, in31
  or or_2 (or_2_out, comparator_2_eq, comparator_3_eq);
  Register #(.width(32)) HI (.D(multiplexer_1_out), .en(or_2_out), .Q(HI_q));  // open: clk, clr
  Register #(.width(32)) LO (.D(multiplexer_2_out), .en(or_2_out), .Q(LO_q));  // open: clk, clr

  // Notes on the sheet:
  //   OP1
  //   OP2
  //   hi
endmodule

module regfile (
  input  [31:0] rd_data,
  input  [4:0] rd,
  input  [4:0] rt,
  input  [4:0] rs,
  input  write_e,
  output [31:0] rs_data,
  output [31:0] rt_data
);

  wire clock_1_out, clock_2_out, clock_3_out, clock_4_out, clock_5_out, clock_6_out, clock_7_out,
       clock_8_out, clock_9_out, clock_10_out, clock_11_out, clock_12_out, clock_13_out, clock_14_out,
       clock_15_out, clock_16_out, clock_17_out, clock_18_out, clock_19_out, clock_20_out, clock_21_out,
       clock_22_out, clock_23_out, clock_24_out, clock_25_out, clock_26_out, clock_27_out, clock_28_out,
       clock_29_out, clock_30_out, clock_32_out, demultiplexer_2_out1, demultiplexer_2_out2,
       demultiplexer_2_out3, demultiplexer_2_out4, demultiplexer_2_out5, demultiplexer_2_out6,
       demultiplexer_2_out7, demultiplexer_2_out8, demultiplexer_2_out9, demultiplexer_2_out10,
       demultiplexer_2_out11, demultiplexer_2_out12, demultiplexer_2_out13, demultiplexer_2_out14,
       demultiplexer_2_out15, demultiplexer_2_out16, demultiplexer_2_out17, demultiplexer_2_out18,
       demultiplexer_2_out19, demultiplexer_2_out20, demultiplexer_2_out21, demultiplexer_2_out22,
       demultiplexer_2_out23, demultiplexer_2_out24, demultiplexer_2_out25, demultiplexer_2_out26,
       demultiplexer_2_out27, demultiplexer_2_out28, demultiplexer_2_out29, demultiplexer_2_out30,
       demultiplexer_2_out31;
  wire [31:0] demultiplexer_1_out1, demultiplexer_1_out2, demultiplexer_1_out3, demultiplexer_1_out4,
       demultiplexer_1_out5, demultiplexer_1_out6, demultiplexer_1_out7, demultiplexer_1_out8,
       demultiplexer_1_out9, demultiplexer_1_out10, demultiplexer_1_out11, demultiplexer_1_out12,
       demultiplexer_1_out13, demultiplexer_1_out14, demultiplexer_1_out15, demultiplexer_1_out16,
       demultiplexer_1_out17, demultiplexer_1_out18, demultiplexer_1_out19, demultiplexer_1_out20,
       demultiplexer_1_out21, demultiplexer_1_out22, demultiplexer_1_out23, demultiplexer_1_out24,
       demultiplexer_1_out25, demultiplexer_1_out26, demultiplexer_1_out27, demultiplexer_1_out28,
       demultiplexer_1_out29, demultiplexer_1_out30, demultiplexer_1_out31, reg1_q, reg2_q, reg3_q, reg4_q,
       reg5_q, reg6_q, reg7_q, reg8_q, reg9_q, reg10_q, reg11_q, reg12_q, reg13_q, reg14_q, reg15_q, reg16_q,
       reg17_q, reg18_q, reg19_q, reg20_q, reg21_q, reg22_q, reg23_q, reg25_q, reg26_q, reg27_q, reg28_q,
       reg29_q, reg30_q, reg31_q, reg32_q;

  Demultiplexer #(.select(5), .width(32)) demultiplexer_1 (
    .out1(demultiplexer_1_out1), .out2(demultiplexer_1_out2), .out3(demultiplexer_1_out3),
    .out4(demultiplexer_1_out4), .out5(demultiplexer_1_out5), .out6(demultiplexer_1_out6),
    .out7(demultiplexer_1_out7), .out8(demultiplexer_1_out8), .out9(demultiplexer_1_out9),
    .out10(demultiplexer_1_out10), .out11(demultiplexer_1_out11), .out12(demultiplexer_1_out12),
    .out13(demultiplexer_1_out13), .out14(demultiplexer_1_out14), .out15(demultiplexer_1_out15),
    .out16(demultiplexer_1_out16), .out17(demultiplexer_1_out17), .out18(demultiplexer_1_out18),
    .out19(demultiplexer_1_out19), .out20(demultiplexer_1_out20), .out21(demultiplexer_1_out21),
    .out22(demultiplexer_1_out22), .out23(demultiplexer_1_out23), .out24(demultiplexer_1_out24),
    .out25(demultiplexer_1_out25), .out26(demultiplexer_1_out26), .out27(demultiplexer_1_out27),
    .out28(demultiplexer_1_out28), .out29(demultiplexer_1_out29), .out30(demultiplexer_1_out30),
    .out31(demultiplexer_1_out31), .in(rd_data), .sel(rd));  // open: out0
  Demultiplexer #(.select(5)) demultiplexer_2 (
    .out1(demultiplexer_2_out1), .out2(demultiplexer_2_out2), .out3(demultiplexer_2_out3),
    .out4(demultiplexer_2_out4), .out5(demultiplexer_2_out5), .out6(demultiplexer_2_out6),
    .out7(demultiplexer_2_out7), .out8(demultiplexer_2_out8), .out9(demultiplexer_2_out9),
    .out10(demultiplexer_2_out10), .out11(demultiplexer_2_out11), .out12(demultiplexer_2_out12),
    .out13(demultiplexer_2_out13), .out14(demultiplexer_2_out14), .out15(demultiplexer_2_out15),
    .out16(demultiplexer_2_out16), .out17(demultiplexer_2_out17), .out18(demultiplexer_2_out18),
    .out19(demultiplexer_2_out19), .out20(demultiplexer_2_out20), .out21(demultiplexer_2_out21),
    .out22(demultiplexer_2_out22), .out23(demultiplexer_2_out23), .out24(demultiplexer_2_out24),
    .out25(demultiplexer_2_out25), .out26(demultiplexer_2_out26), .out27(demultiplexer_2_out27),
    .out28(demultiplexer_2_out28), .out29(demultiplexer_2_out29), .out30(demultiplexer_2_out30),
    .out31(demultiplexer_2_out31), .in(write_e), .sel(rd));  // open: out0
  Register #(.width(32)) reg1 (
    .D(demultiplexer_1_out1), .en(demultiplexer_2_out1), .clk(clock_1_out), .Q(reg1_q));  // open: clr
  Clock clock_1 (.out(clock_1_out));
  Register #(.width(32)) reg2 (
    .D(demultiplexer_1_out2), .en(demultiplexer_2_out2), .clk(clock_2_out), .Q(reg2_q));  // open: clr
  Clock clock_2 (.out(clock_2_out));
  Register #(.width(32)) reg3 (
    .D(demultiplexer_1_out3), .en(demultiplexer_2_out3), .clk(clock_3_out), .Q(reg3_q));  // open: clr
  Clock clock_3 (.out(clock_3_out));
  Register #(.width(32)) reg4 (
    .D(demultiplexer_1_out4), .en(demultiplexer_2_out4), .clk(clock_4_out), .Q(reg4_q));  // open: clr
  Clock clock_4 (.out(clock_4_out));
  Register #(.width(32)) reg5 (
    .D(demultiplexer_1_out5), .en(demultiplexer_2_out5), .clk(clock_5_out), .Q(reg5_q));  // open: clr
  Clock clock_5 (.out(clock_5_out));
  Clock clock_6 (.out(clock_6_out));
  Register #(.width(32)) reg6 (
    .D(demultiplexer_1_out6), .en(demultiplexer_2_out6), .clk(clock_6_out), .Q(reg6_q));  // open: clr
  Register #(.width(32)) reg7 (
    .D(demultiplexer_1_out7), .en(demultiplexer_2_out7), .clk(clock_7_out), .Q(reg7_q));  // open: clr
  Clock clock_7 (.out(clock_7_out));
  Register #(.width(32)) reg8 (
    .D(demultiplexer_1_out8), .en(demultiplexer_2_out8), .clk(clock_8_out), .Q(reg8_q));  // open: clr
  Clock clock_8 (.out(clock_8_out));
  Register #(.width(32)) reg9 (
    .D(demultiplexer_1_out9), .en(demultiplexer_2_out9), .clk(clock_9_out), .Q(reg9_q));  // open: clr
  Clock clock_9 (.out(clock_9_out));
  Register #(.width(32)) reg10 (
    .D(demultiplexer_1_out10), .en(demultiplexer_2_out10), .clk(clock_10_out), .Q(reg10_q));  // open: clr
  Clock clock_10 (.out(clock_10_out));
  Clock clock_11 (.out(clock_11_out));
  Register #(.width(32)) reg11 (
    .D(demultiplexer_1_out11), .en(demultiplexer_2_out11), .clk(clock_11_out), .Q(reg11_q));  // open: clr
  Register #(.width(32)) reg12 (
    .D(demultiplexer_1_out12), .en(demultiplexer_2_out12), .clk(clock_12_out), .Q(reg12_q));  // open: clr
  Clock clock_12 (.out(clock_12_out));
  Register #(.width(32)) reg13 (
    .D(demultiplexer_1_out13), .en(demultiplexer_2_out13), .clk(clock_13_out), .Q(reg13_q));  // open: clr
  Clock clock_13 (.out(clock_13_out));
  Register #(.width(32)) reg14 (
    .D(demultiplexer_1_out14), .en(demultiplexer_2_out14), .clk(clock_14_out), .Q(reg14_q));  // open: clr
  Clock clock_14 (.out(clock_14_out));
  Clock clock_15 (.out(clock_15_out));
  Register #(.width(32)) reg15 (
    .D(demultiplexer_1_out15), .en(demultiplexer_2_out15), .clk(clock_15_out), .Q(reg15_q));  // open: clr
  Register #(.width(32)) reg16 (
    .D(demultiplexer_1_out16), .en(demultiplexer_2_out16), .clk(clock_16_out), .Q(reg16_q));  // open: clr
  Clock clock_16 (.out(clock_16_out));
  Register #(.width(32)) reg17 (
    .D(demultiplexer_1_out17), .en(demultiplexer_2_out17), .clk(clock_17_out), .Q(reg17_q));  // open: clr
  Clock clock_17 (.out(clock_17_out));
  Register #(.width(32)) reg18 (
    .D(demultiplexer_1_out18), .en(demultiplexer_2_out18), .clk(clock_18_out), .Q(reg18_q));  // open: clr
  Clock clock_18 (.out(clock_18_out));
  Clock clock_19 (.out(clock_19_out));
  Register #(.width(32)) reg19 (
    .D(demultiplexer_1_out19), .en(demultiplexer_2_out19), .clk(clock_19_out), .Q(reg19_q));  // open: clr
  Clock clock_20 (.out(clock_20_out));
  Register #(.width(32)) reg20 (
    .D(demultiplexer_1_out20), .en(demultiplexer_2_out20), .clk(clock_20_out), .Q(reg20_q));  // open: clr
  Register #(.width(32)) reg21 (
    .D(demultiplexer_1_out21), .en(demultiplexer_2_out21), .clk(clock_21_out), .Q(reg21_q));  // open: clr
  Clock clock_21 (.out(clock_21_out));
  Register #(.width(32)) reg22 (
    .D(demultiplexer_1_out22), .en(demultiplexer_2_out22), .clk(clock_22_out), .Q(reg22_q));  // open: clr
  Clock clock_22 (.out(clock_22_out));
  Register #(.width(32)) reg23 (
    .D(demultiplexer_1_out23), .en(demultiplexer_2_out23), .clk(clock_23_out), .Q(reg23_q));  // open: clr
  Clock clock_23 (.out(clock_23_out));
  Clock clock_24 (.out(clock_24_out));
  Register #(.width(32)) reg25 (
    .D(demultiplexer_1_out24), .en(demultiplexer_2_out24), .clk(clock_24_out), .Q(reg25_q));  // open: clr
  Register #(.width(32)) reg26 (
    .D(demultiplexer_1_out25), .en(demultiplexer_2_out25), .clk(clock_25_out), .Q(reg26_q));  // open: clr
  Clock clock_25 (.out(clock_25_out));
  Register #(.width(32)) reg27 (
    .D(demultiplexer_1_out26), .en(demultiplexer_2_out26), .clk(clock_26_out), .Q(reg27_q));  // open: clr
  Clock clock_26 (.out(clock_26_out));
  Register #(.width(32)) reg28 (
    .D(demultiplexer_1_out27), .en(demultiplexer_2_out27), .clk(clock_27_out), .Q(reg28_q));  // open: clr
  Clock clock_27 (.out(clock_27_out));
  Clock clock_28 (.out(clock_28_out));
  Register #(.width(32)) reg29 (
    .D(demultiplexer_1_out28), .en(demultiplexer_2_out28), .clk(clock_28_out), .Q(reg29_q));  // open: clr
  Clock clock_29 (.out(clock_29_out));
  Register #(.width(32)) reg30 (
    .D(demultiplexer_1_out29), .en(demultiplexer_2_out29), .clk(clock_29_out), .Q(reg30_q));  // open: clr
  Register #(.width(32)) reg31 (
    .D(demultiplexer_1_out30), .en(demultiplexer_2_out30), .clk(clock_30_out), .Q(reg31_q));  // open: clr
  Clock clock_30 (.out(clock_30_out));
  Clock clock_31 ();  // open: out
  Register #(.width(32)) reg32 (
    .D(demultiplexer_1_out31), .en(demultiplexer_2_out31), .clk(clock_32_out), .Q(reg32_q));  // open: clr
  Clock clock_32 (.out(clock_32_out));
  Multiplexer #(.select(5), .width(32)) multiplexer_1 (
    .in0({32{1'b0}}), .in1(reg1_q), .in2(reg2_q), .in3(reg3_q), .in4(reg4_q), .in5(reg5_q), .in6(reg6_q),
    .in7(reg7_q), .in8(reg8_q), .in9(reg9_q), .in10(reg10_q), .in11(reg11_q), .in12(reg12_q), .in13(reg13_q),
    .in14(reg14_q), .in15(reg15_q), .in16(reg16_q), .in17(reg17_q), .in18(reg18_q), .in19(reg19_q),
    .in20(reg20_q), .in21(reg21_q), .in22(reg22_q), .in23(reg23_q), .in24(reg25_q), .in25(reg26_q),
    .in26(reg27_q), .in27(reg28_q), .in28(reg29_q), .in29(reg30_q), .in30(reg31_q), .in31(reg32_q),
    .out(rs_data), .sel(rt));
  Multiplexer #(.select(5), .width(32)) multiplexer_2 (
    .in0({32{1'b0}}), .in1(reg1_q), .in2(reg2_q), .in3(reg3_q), .in4(reg4_q), .in5(reg5_q), .in6(reg6_q),
    .in7(reg7_q), .in8(reg8_q), .in9(reg9_q), .in10(reg10_q), .in11(reg11_q), .in12(reg12_q), .in13(reg13_q),
    .in14(reg14_q), .in15(reg15_q), .in16(reg16_q), .in17(reg17_q), .in18(reg18_q), .in19(reg19_q),
    .in20(reg20_q), .in21(reg21_q), .in22(reg22_q), .in23(reg23_q), .in24(reg25_q), .in25(reg26_q),
    .in26(reg27_q), .in27(reg28_q), .in28(reg29_q), .in29(reg30_q), .in30(reg31_q), .in31(reg32_q),
    .out(rt_data), .sel(rs));

  // Notes on the sheet:
  //   rs Multi
  //   rt Multi
endmodule

module TESTminiRegFile (
  input  [4:0] rs,
  input  [4:0] rt,
  input  [4:0] rd,
  input  WE,
  input  [31:0] rdData,
  output [31:0] rsData
);

  wire [31:0] reg1_q, reg2_q, reg3_q, reg4_q;

  Register #(.width(32)) reg1 (.Q(reg1_q));  // open: D, en, clk, clr
  Register #(.width(32)) reg2 (.Q(reg2_q));  // open: D, en, clk, clr
  Register #(.width(32)) reg3 (.Q(reg3_q));  // open: D, en, clk, clr
  Register #(.width(32)) reg4 (.Q(reg4_q));  // open: D, en, clk, clr
  Multiplexer #(.select(5), .width(32)) multiplexer_1 (
    .in0({32{1'b0}}), .in1(reg1_q), .in2(reg2_q), .in3(reg3_q), .in4(reg4_q), .sel(rs));  // open: in5, in6, in7, in8, in9, in10, in11, in12, in13, in14, in15, in16, in17, in18, in19, in20, in21, in22, in23, in24, in25, in26, in27, in28, in29, in30, in31, out
endmodule

module Control (
  input  [31:0] Inst,
  output [4:0] rd,
  output [4:0] rt,
  output [4:0] rs,
  output [31:0] imm,
  output reg_write_e,
  output imm_sel,
  output [4:0] ALU_code
);

  wire addcontrol_1_imm_sel, addcontrol_1_reg_write_e, addcontrol_2_imm_sel, addcontrol_2_reg_write_e,
       addisubcircuit_1_imm_sel, addisubcircuit_1_reg_write_e, divcontrol_1_imm_sel,
       divcontrol_1_reg_write_e, mfhisubcircuit_1_imm_sel, mfhisubcircuit_1_reg_write_e,
       mflocontrol_1_imm_sel, mflocontrol_1_reg_write_e, multcontrol_1_imm_sel, multcontrol_1_reg_write_e,
       norcontrol_1_imm_sel, norcontrol_1_reg_write_e, orcontrol_1_imm_sel, orcontrol_1_reg_write_e,
       sllcontrol_1_imm_sel, sllcontrol_1_reg_write_e, sltcontrol_1_imm_sel, sltcontrol_1_reg_write_e,
       srlcontrol_1_imm_sel, srlcontrol_1_reg_write_e, subcontrol_1_imm_sel, subcontrol_1_reg_write_e,
       xorcontrol_1_imm_sel, xorcontrol_1_reg_write_e;
  wire [4:0] addcontrol_1_alu_code, addcontrol_1_rd, addcontrol_1_rs, addcontrol_1_rt, addcontrol_2_alu_code,
       addcontrol_2_rd, addcontrol_2_rs, addcontrol_2_rt, addisubcircuit_1_alu_code, addisubcircuit_1_rd,
       addisubcircuit_1_rs, addisubcircuit_1_rt, divcontrol_1_alu_code, divcontrol_1_rd, divcontrol_1_rs,
       divcontrol_1_rt, mfhisubcircuit_1_alu_code, mfhisubcircuit_1_rd, mfhisubcircuit_1_rs,
       mfhisubcircuit_1_rt, mflocontrol_1_alu_code, mflocontrol_1_rd, mflocontrol_1_rs, mflocontrol_1_rt,
       multcontrol_1_alu_code, multcontrol_1_rd, multcontrol_1_rs, multcontrol_1_rt, norcontrol_1_alu_code,
       norcontrol_1_rd, norcontrol_1_rs, norcontrol_1_rt, orcontrol_1_alu_code, orcontrol_1_rd,
       orcontrol_1_rs, orcontrol_1_rt, sllcontrol_1_alu_code, sllcontrol_1_rd, sllcontrol_1_rs,
       sllcontrol_1_rt, sltcontrol_1_alu_code, sltcontrol_1_rd, sltcontrol_1_rs, sltcontrol_1_rt,
       srlcontrol_1_alu_code, srlcontrol_1_rd, srlcontrol_1_rs, srlcontrol_1_rt, subcontrol_1_alu_code,
       subcontrol_1_rd, subcontrol_1_rs, subcontrol_1_rt, xorcontrol_1_alu_code, xorcontrol_1_rd,
       xorcontrol_1_rs, xorcontrol_1_rt;
  wire [31:0] addcontrol_1_imm, addcontrol_2_imm, addisubcircuit_1_imm, divcontrol_1_imm,
       mfhisubcircuit_1_imm, mflocontrol_1_imm, multcontrol_1_imm, norcontrol_1_imm, orcontrol_1_imm,
       sixbitdemultiplexor_1_add, sixbitdemultiplexor_1_addi, sixbitdemultiplexor_1_andoutput,
       sixbitdemultiplexor_1_div, sixbitdemultiplexor_1_mfhi, sixbitdemultiplexor_1_mflo,
       sixbitdemultiplexor_1_mult, sixbitdemultiplexor_1_noroutput, sixbitdemultiplexor_1_oroutput,
       sixbitdemultiplexor_1_shiftll, sixbitdemultiplexor_1_shiftrl, sixbitdemultiplexor_1_slt,
       sixbitdemultiplexor_1_sub, sixbitdemultiplexor_1_xoroutput, sllcontrol_1_imm, sltcontrol_1_imm,
       srlcontrol_1_imm, subcontrol_1_imm, xorcontrol_1_imm;

  sixBitDemultiplexor sixbitdemultiplexor_1 (
    .data(Inst), .add(sixbitdemultiplexor_1_add), .sub(sixbitdemultiplexor_1_sub),
    .mult(sixbitdemultiplexor_1_mult), .div(sixbitdemultiplexor_1_div), .mflo(sixbitdemultiplexor_1_mflo),
    .mfhi(sixbitdemultiplexor_1_mfhi), .shiftll(sixbitdemultiplexor_1_shiftll),
    .shiftrl(sixbitdemultiplexor_1_shiftrl), .slt(sixbitdemultiplexor_1_slt),
    .andOutput(sixbitdemultiplexor_1_andoutput), .orOutput(sixbitdemultiplexor_1_oroutput),
    .norOutput(sixbitdemultiplexor_1_noroutput), .xorOutput(sixbitdemultiplexor_1_xoroutput),
    .addi(sixbitdemultiplexor_1_addi));
  addControl addcontrol_1 (
    .data(sixbitdemultiplexor_1_add), .rd(addcontrol_1_rd), .rt(addcontrol_1_rt), .rs(addcontrol_1_rs),
    .imm(addcontrol_1_imm), .reg_write_e(addcontrol_1_reg_write_e), .imm_sel(addcontrol_1_imm_sel),
    .ALU_code(addcontrol_1_alu_code));
  subControl subcontrol_1 (
    .data(sixbitdemultiplexor_1_sub), .rd(subcontrol_1_rd), .rt(subcontrol_1_rt), .rs(subcontrol_1_rs),
    .imm(subcontrol_1_imm), .reg_write_e(subcontrol_1_reg_write_e), .imm_sel(subcontrol_1_imm_sel),
    .ALU_code(subcontrol_1_alu_code));
  multControl multcontrol_1 (
    .data(sixbitdemultiplexor_1_mult), .rd(multcontrol_1_rd), .rt(multcontrol_1_rt), .rs(multcontrol_1_rs),
    .imm(multcontrol_1_imm), .reg_write_e(multcontrol_1_reg_write_e), .imm_sel(multcontrol_1_imm_sel),
    .ALU_code(multcontrol_1_alu_code));
  divControl divcontrol_1 (
    .data(sixbitdemultiplexor_1_div), .rd(divcontrol_1_rd), .rt(divcontrol_1_rt), .rs(divcontrol_1_rs),
    .imm(divcontrol_1_imm), .reg_write_e(divcontrol_1_reg_write_e), .imm_sel(divcontrol_1_imm_sel),
    .ALU_code(divcontrol_1_alu_code));
  mfloControl mflocontrol_1 (
    .data(sixbitdemultiplexor_1_mflo), .rd(mflocontrol_1_rd), .rt(mflocontrol_1_rt), .rs(mflocontrol_1_rs),
    .imm(mflocontrol_1_imm), .reg_write_e(mflocontrol_1_reg_write_e), .imm_sel(mflocontrol_1_imm_sel),
    .ALU_code(mflocontrol_1_alu_code));
  mfhiSubcircuit mfhisubcircuit_1 (
    .in_1(sixbitdemultiplexor_1_mfhi), .rs(mfhisubcircuit_1_rs), .rt(mfhisubcircuit_1_rt),
    .rd(mfhisubcircuit_1_rd), .imm(mfhisubcircuit_1_imm), .reg_write_e(mfhisubcircuit_1_reg_write_e),
    .imm_sel(mfhisubcircuit_1_imm_sel), .ALU_code(mfhisubcircuit_1_alu_code));
  sllControl sllcontrol_1 (
    .data(sixbitdemultiplexor_1_shiftll), .imm(sllcontrol_1_imm), .rd(sllcontrol_1_rd), .rt(sllcontrol_1_rt),
    .rs(sllcontrol_1_rs), .reg_write_e(sllcontrol_1_reg_write_e), .imm_sel(sllcontrol_1_imm_sel),
    .ALU_code(sllcontrol_1_alu_code));
  srlControl srlcontrol_1 (
    .data(sixbitdemultiplexor_1_shiftrl), .imm(srlcontrol_1_imm), .rd(srlcontrol_1_rd), .rt(srlcontrol_1_rt),
    .rs(srlcontrol_1_rs), .reg_write_e(srlcontrol_1_reg_write_e), .imm_sel(srlcontrol_1_imm_sel),
    .ALU_code(srlcontrol_1_alu_code));
  sltControl sltcontrol_1 (
    .data(sixbitdemultiplexor_1_slt), .rd(sltcontrol_1_rd), .rt(sltcontrol_1_rt), .rs(sltcontrol_1_rs),
    .imm(sltcontrol_1_imm), .reg_write_e(sltcontrol_1_reg_write_e), .imm_sel(sltcontrol_1_imm_sel),
    .ALU_code(sltcontrol_1_alu_code));
  addControl addcontrol_2 (
    .data(sixbitdemultiplexor_1_andoutput), .rd(addcontrol_2_rd), .rt(addcontrol_2_rt), .rs(addcontrol_2_rs),
    .imm(addcontrol_2_imm), .reg_write_e(addcontrol_2_reg_write_e), .imm_sel(addcontrol_2_imm_sel),
    .ALU_code(addcontrol_2_alu_code));
  orControl orcontrol_1 (
    .data(sixbitdemultiplexor_1_oroutput), .rd(orcontrol_1_rd), .rt(orcontrol_1_rt), .rs(orcontrol_1_rs),
    .imm(orcontrol_1_imm), .reg_write_e(orcontrol_1_reg_write_e), .imm_sel(orcontrol_1_imm_sel),
    .ALU_code(orcontrol_1_alu_code));
  xorControl xorcontrol_1 (
    .data(sixbitdemultiplexor_1_xoroutput), .rd(xorcontrol_1_rd), .rt(xorcontrol_1_rt), .rs(xorcontrol_1_rs),
    .imm(xorcontrol_1_imm), .reg_write_e(xorcontrol_1_reg_write_e), .imm_sel(xorcontrol_1_imm_sel),
    .ALU_code(xorcontrol_1_alu_code));
  norControl norcontrol_1 (
    .data(sixbitdemultiplexor_1_noroutput), .rd(norcontrol_1_rd), .rt(norcontrol_1_rt), .rs(norcontrol_1_rs),
    .imm(norcontrol_1_imm), .reg_write_e(norcontrol_1_reg_write_e), .imm_sel(norcontrol_1_imm_sel),
    .ALU_code(norcontrol_1_alu_code));
  addiSubcircuit addisubcircuit_1 (
    .in_1(sixbitdemultiplexor_1_addi), .rs(addisubcircuit_1_rs), .rt(addisubcircuit_1_rt),
    .rd(addisubcircuit_1_rd), .imm(addisubcircuit_1_imm), .reg_write_e(addisubcircuit_1_reg_write_e),
    .imm_sel(addisubcircuit_1_imm_sel), .ALU_code(addisubcircuit_1_alu_code));
  assign rd = mfhisubcircuit_1_rd | mflocontrol_1_rd | addcontrol_1_rd | subcontrol_1_rd | multcontrol_1_rd | divcontrol_1_rd | sllcontrol_1_rd | srlcontrol_1_rd | sltcontrol_1_rd | addcontrol_2_rd | orcontrol_1_rd | xorcontrol_1_rd | norcontrol_1_rd | addisubcircuit_1_rd;  // OR_Gate or_1, 5 bits wide
  assign rt = sltcontrol_1_rt | addcontrol_2_rt | orcontrol_1_rt | xorcontrol_1_rt | norcontrol_1_rt | addisubcircuit_1_rt | addcontrol_1_rt | subcontrol_1_rt | multcontrol_1_rt | divcontrol_1_rt | mflocontrol_1_rt | mfhisubcircuit_1_rt | sllcontrol_1_rt | srlcontrol_1_rt;  // OR_Gate or_2, 5 bits wide
  assign rs = addcontrol_1_rs | subcontrol_1_rs | multcontrol_1_rs | divcontrol_1_rs | mflocontrol_1_rs | mfhisubcircuit_1_rs | sllcontrol_1_rs | srlcontrol_1_rs | sltcontrol_1_rs | addcontrol_2_rs | orcontrol_1_rs | xorcontrol_1_rs | norcontrol_1_rs | addisubcircuit_1_rs;  // OR_Gate or_3, 5 bits wide
  assign imm = addcontrol_1_imm | subcontrol_1_imm | multcontrol_1_imm | divcontrol_1_imm | mflocontrol_1_imm | mfhisubcircuit_1_imm | sllcontrol_1_imm | srlcontrol_1_imm | sltcontrol_1_imm | addcontrol_2_imm | orcontrol_1_imm | xorcontrol_1_imm | norcontrol_1_imm | addisubcircuit_1_imm;  // OR_Gate or_4, 32 bits wide
  or or_5 (reg_write_e, addcontrol_1_reg_write_e, subcontrol_1_reg_write_e, multcontrol_1_reg_write_e, divcontrol_1_reg_write_e, mflocontrol_1_reg_write_e, mfhisubcircuit_1_reg_write_e, sllcontrol_1_reg_write_e, srlcontrol_1_reg_write_e, sltcontrol_1_reg_write_e, addcontrol_2_reg_write_e, orcontrol_1_reg_write_e, xorcontrol_1_reg_write_e, norcontrol_1_reg_write_e, addisubcircuit_1_reg_write_e);
  or or_6 (imm_sel, addcontrol_1_imm_sel, subcontrol_1_imm_sel, multcontrol_1_imm_sel, divcontrol_1_imm_sel, mflocontrol_1_imm_sel, mfhisubcircuit_1_imm_sel, sllcontrol_1_imm_sel, srlcontrol_1_imm_sel, sltcontrol_1_imm_sel, addcontrol_2_imm_sel, orcontrol_1_imm_sel, xorcontrol_1_imm_sel, norcontrol_1_imm_sel, addisubcircuit_1_imm_sel);
  assign ALU_code = addcontrol_1_alu_code | subcontrol_1_alu_code | multcontrol_1_alu_code | divcontrol_1_alu_code | mflocontrol_1_alu_code | mfhisubcircuit_1_alu_code | sllcontrol_1_alu_code | srlcontrol_1_alu_code | sltcontrol_1_alu_code | addcontrol_2_alu_code | orcontrol_1_alu_code | xorcontrol_1_alu_code | norcontrol_1_alu_code | addisubcircuit_1_alu_code;  // OR_Gate or_7, 5 bits wide

  // Notes on the sheet:
  //   rd
endmodule

module addControl (
  input  [31:0] data,
  output [4:0] rd,
  output [4:0] rt,
  output [4:0] rs,
  output [31:0] imm,
  output reg_write_e,
  output imm_sel,
  output [4:0] ALU_code
);

  wire comparator_1_gt;

  Comparator #(.mode("unsigned"), .width(32)) comparator_1 (
    .a(data), .b({32{1'b0}}), .gt(comparator_1_gt));  // open: eq, lt
  Multiplexer multiplexer_1 (.in0(1'b1), .in1(1'b0), .out(reg_write_e), .sel(comparator_1_gt));

  assign ALU_code = {5{1'b0}};
  assign imm = {32{1'b0}};
  assign imm_sel = 1'b0;
  assign rd = data[15:11];
  assign rs = data[25:21];
  assign rt = data[20:16];
endmodule

module sixBitDemultiplexor (
  input  [31:0] data,
  output [31:0] add,
  output [31:0] sub,
  output [31:0] mult,
  output [31:0] div,
  output [31:0] mflo,
  output [31:0] mfhi,
  output [31:0] shiftll,
  output [31:0] shiftrl,
  output [31:0] slt,
  output [31:0] andOutput,
  output [31:0] orOutput,
  output [31:0] norOutput,
  output [31:0] xorOutput,
  output [31:0] addi
);

  wire demultiplexer_1_out0, demultiplexer_2_out0, demultiplexer_2_out1, demultiplexer_3_out0,
       demultiplexer_3_out2, demultiplexer_3_out4, demultiplexer_3_out5, demultiplexer_3_out6,
       demultiplexer_3_out7, demultiplexer_4_out0, demultiplexer_4_out2, demultiplexer_4_out3,
       demultiplexer_4_out4, demultiplexer_4_out5, functAdd100000_out, functAND100100_out,
       functDiv011010_out, functMfhi010000_out, functMflo010010_out, functMult011000_out, functNOR100111_out,
       functOR100101_out, functSll000000_out, functSlt101010_out, functSrl000010_out, functSub100010_out,
       functXOR100110_out, opcode000000_out, opcode001000_out;
  wire [31:0] undriven;

  Demultiplexer #(.select(3)) demultiplexer_1 (
    .out0(demultiplexer_1_out0), .in(1'b1), .sel(data[28:26]));  // open: out1, out2, out3, out4, out5, out6, out7
  Demultiplexer #(.select(3)) demultiplexer_2 (
    .out0(demultiplexer_2_out0), .out1(demultiplexer_2_out1), .in(1'b1), .sel(data[31:29]));  // open: out2, out3, out4, out5, out6, out7
  and opcode000000 (opcode000000_out, demultiplexer_1_out0, demultiplexer_2_out0);
  and opcode001000 (opcode001000_out, demultiplexer_2_out1, demultiplexer_1_out0);
  Demultiplexer #(.select(3)) demultiplexer_3 (
    .out0(demultiplexer_3_out0), .out2(demultiplexer_3_out2), .out4(demultiplexer_3_out4),
    .out5(demultiplexer_3_out5), .out6(demultiplexer_3_out6), .out7(demultiplexer_3_out7),
    .in(opcode000000_out), .sel(data[2:0]));  // open: out1, out3
  Demultiplexer #(.select(3)) demultiplexer_4 (
    .out0(demultiplexer_4_out0), .out2(demultiplexer_4_out2), .out3(demultiplexer_4_out3),
    .out4(demultiplexer_4_out4), .out5(demultiplexer_4_out5), .in(opcode000000_out), .sel(data[5:3]));  // open: out1, out6, out7
  Multiplexer #(.width(32)) multiplexer_1 (.in0({32{1'b0}}), .in1(data), .out(addi), .sel(opcode001000_out));
  and functAdd100000 (functAdd100000_out, demultiplexer_3_out0, demultiplexer_4_out4);
  and functSub100010 (functSub100010_out, demultiplexer_3_out2, demultiplexer_4_out4);
  and functMult011000 (functMult011000_out, demultiplexer_3_out0, demultiplexer_4_out3);
  and functDiv011010 (functDiv011010_out, demultiplexer_3_out2, demultiplexer_4_out3);
  and functMflo010010 (functMflo010010_out, demultiplexer_3_out2, demultiplexer_4_out2);
  and functMfhi010000 (functMfhi010000_out, demultiplexer_3_out0, demultiplexer_4_out2);
  and functSll000000 (functSll000000_out, demultiplexer_3_out0, demultiplexer_4_out0);
  and functSrl000010 (functSrl000010_out, demultiplexer_3_out2, demultiplexer_4_out0);
  and functSlt101010 (functSlt101010_out, demultiplexer_3_out2, demultiplexer_4_out5);
  and functAND100100 (functAND100100_out, demultiplexer_4_out4, demultiplexer_3_out4);
  and functOR100101 (functOR100101_out, demultiplexer_4_out4, demultiplexer_3_out5);
  and functNOR100111 (functNOR100111_out, demultiplexer_4_out4, demultiplexer_3_out7);
  and functXOR100110 (functXOR100110_out, demultiplexer_4_out4, demultiplexer_3_out6);
  Multiplexer #(.width(32)) multiplexer_2 (.in0({32{1'b0}}), .in1(data), .out(add), .sel(functAdd100000_out));
  Multiplexer #(.width(32)) multiplexer_3 (.in0({32{1'b0}}), .in1(data), .out(sub), .sel(functSub100010_out));
  Multiplexer #(.width(32)) multiplexer_4 (.in0({32{1'b0}}), .in1(data), .out(mult), .sel(functMult011000_out));
  Multiplexer #(.width(32)) multiplexer_5 (.in0({32{1'b0}}), .in1(data), .out(div), .sel(functDiv011010_out));
  Multiplexer #(.width(32)) multiplexer_6 (.in0({32{1'b0}}), .in1(data), .out(mflo), .sel(functMflo010010_out));
  Multiplexer #(.width(32)) multiplexer_7 (.in0({32{1'b0}}), .in1(data), .out(mfhi), .sel(functMfhi010000_out));
  Multiplexer #(.width(32)) multiplexer_8 (.in0({32{1'b0}}), .in1(data), .out(shiftll), .sel(functSll000000_out));
  Multiplexer #(.width(32)) multiplexer_9 (.in0({32{1'b0}}), .in1(data), .out(shiftrl), .sel(functSrl000010_out));
  Multiplexer #(.width(32)) multiplexer_10 (.in0(undriven), .in1(data), .out(slt), .sel(functSlt101010_out));
  Multiplexer #(.width(32)) multiplexer_11 (.in0({32{1'b0}}), .in1(data), .out(andOutput), .sel(functAND100100_out));
  Multiplexer #(.width(32)) multiplexer_12 (.in0({32{1'b0}}), .in1(data), .out(orOutput), .sel(functOR100101_out));
  Multiplexer #(.width(32)) multiplexer_13 (.in0({32{1'b0}}), .in1(data), .out(norOutput), .sel(functNOR100111_out));
  Multiplexer #(.width(32)) multiplexer_14 (.in0({32{1'b0}}), .in1(data), .out(xorOutput), .sel(functXOR100110_out));

  // Notes on the sheet:
  //   funct code
  //   opcode
  //   order of demultiplexors
  //   000
  //   001
  //   010
  //   011
  //   100
  //   101
  //   110
  //   111
  //   lower order bits
  //   higher order bits
  //   order of demultiplexors
  //   output0 000
  //   output1 001
  //   output2 010
  //   output3 011
  //   output4 100
  //   output5 101
  //   output6 110
  //   output7 111
  //   lower order bits
  //   data
  //   need multiplexor to give which funct code is matching the funct code given
  //   higher order bits
  //   data
endmodule

module subControl (
  input  [31:0] data,
  output [4:0] rd,
  output [4:0] rt,
  output [4:0] rs,
  output [31:0] imm,
  output reg_write_e,
  output imm_sel,
  output [4:0] ALU_code
);

  wire comparator_1_gt;

  Comparator #(.mode("unsigned"), .width(32)) comparator_1 (
    .a(data), .b({32{1'b0}}), .gt(comparator_1_gt));  // open: eq, lt
  Multiplexer multiplexer_1 (.in0(1'b1), .in1(1'b0), .out(reg_write_e), .sel(comparator_1_gt));

  assign ALU_code = 5'b00001;
  assign imm = {32{1'b0}};
  assign imm_sel = 1'b0;
  assign rd = data[15:11];
  assign rs = data[25:21];
  assign rt = data[20:16];
endmodule

module mfloControl (
  input  [31:0] data,
  output [4:0] rd,
  output [4:0] rt,
  output [4:0] rs,
  output [31:0] imm,
  output reg_write_e,
  output imm_sel,
  output [4:0] ALU_code
);

  wire comparator_1_gt;

  Comparator #(.mode("unsigned"), .width(32)) comparator_1 (
    .a(data), .b({32{1'b0}}), .gt(comparator_1_gt));  // open: eq, lt
  Multiplexer multiplexer_1 (.in0(1'b1), .in1(1'b0), .out(reg_write_e), .sel(comparator_1_gt));
  Multiplexer #(.width(5)) multiplexer_2 (.in0(5'b00100), .in1({5{1'b0}}), .out(ALU_code), .sel(comparator_1_gt));

  assign imm = {32{1'b0}};
  assign imm_sel = 1'b0;
  assign rd = data[15:11];
  assign rs = {5{1'b0}};
  assign rt = {5{1'b0}};
endmodule

module multControl (
  input  [31:0] data,
  output [4:0] rd,
  output [4:0] rt,
  output [4:0] rs,
  output [31:0] imm,
  output reg_write_e,
  output imm_sel,
  output [4:0] ALU_code
);

  wire comparator_1_gt;

  Comparator #(.mode("unsigned"), .width(32)) comparator_1 (
    .a(data), .b({32{1'b0}}), .gt(comparator_1_gt));  // open: eq, lt
  Multiplexer #(.width(5)) multiplexer_1 (.in0(5'b00010), .in1({5{1'b0}}), .out(ALU_code), .sel(comparator_1_gt));

  assign imm = {32{1'b0}};
  assign imm_sel = 1'b0;
  assign rd = {5{1'b0}};
  assign reg_write_e = 1'b0;
  assign rs = data[25:21];
  assign rt = data[20:16];
endmodule

module srlControl (
  input  [31:0] data,
  output [31:0] imm,
  output [4:0] rd,
  output [4:0] rt,
  output [4:0] rs,
  output reg_write_e,
  output imm_sel,
  output [4:0] ALU_code
);

  wire comparator_1_gt;

  Comparator #(.mode("unsigned"), .width(32)) comparator_1 (
    .a(data), .b({32{1'b0}}), .gt(comparator_1_gt));  // open: eq, lt
  assign imm = {{27{data[10]}}, data[10:6]};  // Bit_Extender bit_extender_1
  Multiplexer #(.width(5)) multiplexer_1 (.in0(5'b00111), .in1({5{1'b0}}), .out(ALU_code), .sel(comparator_1_gt));
  Multiplexer multiplexer_2 (.in0(1'b1), .in1(1'b0), .out(reg_write_e), .sel(comparator_1_gt));
  Multiplexer multiplexer_3 (.in0(1'b1), .in1(1'b0), .out(imm_sel), .sel(comparator_1_gt));

  assign rd = data[15:11];
  assign rs = data[25:21];
  assign rt = data[20:16];
endmodule

module divControl (
  input  [31:0] data,
  output [4:0] rd,
  output [4:0] rt,
  output [4:0] rs,
  output [31:0] imm,
  output reg_write_e,
  output imm_sel,
  output [4:0] ALU_code
);

  wire comparator_1_gt;

  Comparator #(.mode("unsigned"), .width(32)) comparator_1 (
    .a(data), .b({32{1'b0}}), .gt(comparator_1_gt));  // open: eq, lt
  Multiplexer #(.width(5)) multiplexer_1 (.in0(5'b00011), .in1({5{1'b0}}), .out(ALU_code), .sel(comparator_1_gt));

  assign imm = {32{1'b0}};
  assign imm_sel = 1'b0;
  assign rd = {5{1'b0}};
  assign reg_write_e = 1'b0;
  assign rs = data[25:21];
  assign rt = data[20:16];
endmodule

module sllControl (
  input  [31:0] data,
  output [31:0] imm,
  output [4:0] rd,
  output [4:0] rt,
  output [4:0] rs,
  output reg_write_e,
  output imm_sel,
  output [4:0] ALU_code
);

  wire comparator_1_gt;

  Comparator #(.mode("unsigned"), .width(32)) comparator_1 (
    .a(data), .b({32{1'b0}}), .gt(comparator_1_gt));  // open: eq, lt
  assign imm = {{27{data[10]}}, data[10:6]};  // Bit_Extender bit_extender_1
  Multiplexer #(.width(5)) multiplexer_1 (.in0(5'b00110), .in1({5{1'b0}}), .out(ALU_code), .sel(comparator_1_gt));
  Multiplexer multiplexer_2 (.in0(1'b1), .in1(1'b0), .out(reg_write_e), .sel(comparator_1_gt));
  Multiplexer multiplexer_3 (.in0(1'b1), .in1(1'b0), .out(imm_sel), .sel(comparator_1_gt));

  assign rd = data[15:11];
  assign rs = data[25:21];
  assign rt = data[20:16];
endmodule

module orControl (
  input  [31:0] data,
  output [4:0] rd,
  output [4:0] rt,
  output [4:0] rs,
  output [31:0] imm,
  output reg_write_e,
  output imm_sel,
  output [4:0] ALU_code
);

  wire comparator_1_gt;

  Comparator #(.mode("unsigned"), .width(32)) comparator_1 (
    .a(data), .b({32{1'b0}}), .gt(comparator_1_gt));  // open: eq, lt
  Multiplexer multiplexer_1 (.in0(1'b1), .in1(1'b0), .out(reg_write_e), .sel(comparator_1_gt));
  Multiplexer #(.width(5)) multiplexer_2 (.in0(5'b01000), .in1({5{1'b0}}), .out(ALU_code), .sel(comparator_1_gt));

  assign imm = {32{1'b0}};
  assign imm_sel = 1'b0;
  assign rd = data[15:11];
  assign rs = data[25:21];
  assign rt = data[20:16];
endmodule

module addiControl (
  input  [31:0] in_1,
  output [4:0] rs,
  output [4:0] rt,
  output [4:0] rd,
  output [31:0] imm,
  output reg_write_e,
  output imm_sel,
  output [4:0] ALU_code
);

  wire comparator_1_gt;

  Comparator #(.mode("unsigned"), .width(32)) comparator_1 (
    .a(in_1), .b({32{1'b0}}), .gt(comparator_1_gt));  // open: eq, lt
  assign imm = {{16{1'b0}}, in_1[15:0]};  // Bit_Extender bit_extender_1
  Multiplexer multiplexer_1 (.in0(1'b1), .in1(1'b0), .out(reg_write_e), .sel(comparator_1_gt));
  Multiplexer multiplexer_2 (.in0(1'b1), .in1(1'b0), .out(imm_sel), .sel(comparator_1_gt));
  Multiplexer #(.width(5)) multiplexer_3 (.in0({5{1'b0}}), .in1({5{1'b0}}), .out(ALU_code), .sel(comparator_1_gt));

  assign rd = in_1[20:16];
  assign rs = in_1[25:21];
  assign rt = {5{1'b0}};
endmodule

module andControl (
  input  [31:0] data,
  output [4:0] rd,
  output [4:0] rt,
  output [4:0] rs,
  output [31:0] imm,
  output reg_write_e,
  output imm_sel,
  output [4:0] ALU_code
);

  wire comparator_1_gt;

  Comparator #(.mode("unsigned"), .width(32)) comparator_1 (
    .a(data), .b({32{1'b0}}), .gt(comparator_1_gt));  // open: eq, lt
  Multiplexer multiplexer_1 (.in0(1'b1), .in1(1'b0), .out(reg_write_e), .sel(comparator_1_gt));
  Multiplexer #(.width(5)) multiplexer_2 (.in0(5'b01011), .in1({5{1'b0}}), .out(ALU_code), .sel(comparator_1_gt));
  Multiplexer multiplexer_3 (.in0(1'b1), .in1(1'b0), .out(imm_sel), .sel(comparator_1_gt));

  assign imm = {32{1'b0}};
  assign rd = data[15:11];
  assign rs = data[25:21];
  assign rt = data[20:16];
endmodule

module mfhiControl (
  input  [31:0] in_1,
  output [4:0] rs,
  output [4:0] rt,
  output [4:0] rd,
  output [31:0] imm,
  output reg_write_e,
  output imm_sel,
  output [4:0] ALU_code
);

  wire comparator_1_gt;

  Comparator #(.mode("unsigned"), .width(32)) comparator_1 (
    .a(in_1), .b({32{1'b0}}), .gt(comparator_1_gt));  // open: eq, lt
  Multiplexer multiplexer_1 (.in0(1'b1), .in1(1'b0), .out(reg_write_e), .sel(comparator_1_gt));
  Multiplexer #(.width(5)) multiplexer_2 (.in0(5'b00101), .in1({5{1'b0}}), .out(ALU_code), .sel(comparator_1_gt));

  assign imm = {32{1'b0}};
  assign imm_sel = 1'b0;
  assign rd = in_1[20:16];
  assign rs = {5{1'b0}};
  assign rt = {5{1'b0}};
endmodule

module norControl (
  input  [31:0] data,
  output [4:0] rd,
  output [4:0] rt,
  output [4:0] rs,
  output [31:0] imm,
  output reg_write_e,
  output imm_sel,
  output [4:0] ALU_code
);

  wire comparator_1_gt;

  Comparator #(.mode("unsigned"), .width(32)) comparator_1 (
    .a(data), .b({32{1'b0}}), .gt(comparator_1_gt));  // open: eq, lt
  Multiplexer multiplexer_1 (.in0(1'b1), .in1(1'b0), .out(reg_write_e), .sel(comparator_1_gt));
  Multiplexer #(.width(5)) multiplexer_2 (.in0(5'b01001), .in1({5{1'b0}}), .out(ALU_code), .sel(comparator_1_gt));

  assign imm = {32{1'b0}};
  assign imm_sel = 1'b0;
  assign rd = data[15:11];
  assign rs = data[25:21];
  assign rt = data[20:16];
endmodule

module xorControl (
  input  [31:0] data,
  output [4:0] rd,
  output [4:0] rt,
  output [4:0] rs,
  output [31:0] imm,
  output reg_write_e,
  output imm_sel,
  output [4:0] ALU_code
);

  wire comparator_1_gt;

  Comparator #(.mode("unsigned"), .width(32)) comparator_1 (
    .a(data), .b({32{1'b0}}), .gt(comparator_1_gt));  // open: eq, lt
  Multiplexer multiplexer_1 (.in0(1'b1), .in1(1'b0), .out(reg_write_e), .sel(comparator_1_gt));
  Multiplexer #(.width(5)) multiplexer_2 (.in0(5'b01010), .in1({5{1'b0}}), .out(ALU_code), .sel(comparator_1_gt));

  assign imm = {32{1'b0}};
  assign imm_sel = 1'b0;
  assign rd = data[15:11];
  assign rs = data[25:21];
  assign rt = data[20:16];
endmodule

module sltControl (
  input  [31:0] data,
  output [4:0] rd,
  output [4:0] rt,
  output [4:0] rs,
  output [31:0] imm,
  output reg_write_e,
  output imm_sel,
  output [4:0] ALU_code
);

  wire comparator_1_gt;

  Comparator #(.mode("unsigned"), .width(32)) comparator_1 (
    .a(data), .b({32{1'b0}}), .gt(comparator_1_gt));  // open: eq, lt
  Multiplexer multiplexer_1 (.in0(1'b1), .in1(1'b0), .out(reg_write_e), .sel(comparator_1_gt));
  Multiplexer #(.width(5)) multiplexer_2 (.in0(5'b01100), .in1({5{1'b0}}), .out(ALU_code), .sel(comparator_1_gt));

  assign imm = {32{1'b0}};
  assign imm_sel = 1'b0;
  assign rd = data[15:11];
  assign rs = data[25:21];
  assign rt = data[20:16];
endmodule

module addiSubcircuit (
  input  [31:0] in_1,
  output [4:0] rs,
  output [4:0] rt,
  output [4:0] rd,
  output [31:0] imm,
  output reg_write_e,
  output imm_sel,
  output [4:0] ALU_code
);

  assign imm = {{16{1'b0}}, in_1[15:0]};  // Bit_Extender bit_extender_1

  assign ALU_code = 5'b00011;
  assign imm_sel = 1'b1;
  assign rd = in_1[20:16];
  assign reg_write_e = 1'b1;
  assign rs = in_1[25:21];
  assign rt = {5{1'b0}};
endmodule

module mfhiSubcircuit (
  input  [31:0] in_1,
  output [4:0] rs,
  output [4:0] rt,
  output [4:0] rd,
  output [31:0] imm,
  output reg_write_e,
  output imm_sel,
  output [4:0] ALU_code
);

  srlControl srlcontrol_1 ();  // open: data, imm, rd, rt, rs, reg_write_e, imm_sel, ALU_code

  assign ALU_code = 5'b00110;
  assign imm = {32{1'b0}};
  assign imm_sel = 1'b0;
  assign rd = in_1[20:16];
  assign reg_write_e = 1'b1;
  assign rs = {5{1'b0}};
  assign rt = {5{1'b0}};
endmodule
