// Logisim project xorAndNorSubcircuits.circ as structural Verilog: 9 circuits, main circuit regfile
module CPUmain (
);

  regfile regfile_1 ();  // open: rt, rd, rd_data, write_e, rs, rs_data, rt_data
  Control control_1 ();  // open: Inst, rs, rt, rd, imm, reg_write_e, imm_sel, ALU_code
  ALU alu_1 ();  // open: OP1, OP2, ALU_CODE, Res
endmodule

module regfile (
  input  [4:0] rs,
  input  [4:0] rt,
  input  [4:0] rd,
  input  write_e,
  input  [31:0] rd_data,
  output [31:0] rs_data,
  output [31:0] rt_data
);
endmodule

module ALU (
  input  [3:0] ALU_CODE,
  input  [31:0] OP1,
  input  [31:0] OP2,
  output Res
);

  Adder adder_1 ();  // open: a, b, out, cin, cout
  Subtractor subtractor_1 ();  // open: a, b, out, bin, bout
  Multiplier multiplier_1 ();  // open: a, b, out, cin, cout
  Divider divider_1 ();  // open: a, b, out, upper, rem
  Register HI ();  // open: D, en, clk, Q, clr
  Register LO ();  // open: D, en, clk, Q, clr
endmodule

module Control (
  input  [31:0] Inst,
  output [4:0] rs,
  output [4:0] rt,
  output [4:0] rd,
  output [31:0] imm,
  output reg_write_e,
  output imm_sel,
  output [3:0] ALU_code
);

  sixBitDemultiplexor sixbitdemultiplexor_1 (.data(Inst));  // open: add, sub, mult, div, mflo, mfhi, shiftll, shiftrl, slt, addi
endmodule

module sixBitDemultiplexor (
  input  [31:0] data,
  output [31:0] add,
  output [31:0] sub,
  output [31:0] mult,
  output [31:0] div,
  output [31:0] mflo,
  output [31:0] mfhi,
  output [31:0] shiftll,
  output [31:0] shiftrl,
  output [31:0] slt,
  output [31:0] addi
);

  wire demultiplexer_1_out0, demultiplexer_2_out0, demultiplexer_2_out1, demultiplexer_3_out0,
       demultiplexer_3_out2, demultiplexer_4_out0, demultiplexer_4_out2, demultiplexer_4_out3,
       demultiplexer_4_out4, demultiplexer_4_out5, functAdd100000_out, functDiv011010_out,
       functMfhi010000_out, functMflo010010_out, functMult011000_out, functSll000000_out, functSlt101010_out,
       functSrl000010_out, functSub100010_out, opcode000000_out, opcode001000_out;

  Demultiplexer #(.select(3)) demultiplexer_1 (
    .out0(demultiplexer_1_out0), .in(1'b1), .sel(data[28:26]));  // open: out1, out2, out3, out4, out5, out6, out7
  Demultiplexer #(.select(3)) demultiplexer_2 (
    .out0(demultiplexer_2_out0), .out1(demultiplexer_2_out1), .in(1'b1), .sel(data[31:29]));  // open: out2, out3, out4, out5, out6, out7
  and opcode000000 (opcode000000_out, demultiplexer_1_out0, demultiplexer_2_out0);
  and opcode001000 (opcode001000_out, demultiplexer_2_out1, demultiplexer_1_out0);
  Demultiplexer #(.select(3)) demultiplexer_3 (
    .out0(demultiplexer_3_out0), .out2(demultiplexer_3_out2), .in(opcode000000_out), .sel(data[2:0]));  // open: out1, out3, out4, out5, out6, out7
  Demultiplexer #(.select(3)) demultiplexer_4 (
    .out0(demultiplexer_4_out0), .out2(demultiplexer_4_out2), .out3(demultiplexer_4_out3),
    .out4(demultiplexer_4_out4), .out5(demultiplexer_4_out5), .in(opcode000000_out), .sel(data[5:3]));  // open: out1, out6, out7
  Multiplexer #(.width(32)) multiplexer_1 (.in0({32{1'b0}}), .in1(data), .out(addi), .sel(opcode001000_out));
  and functAdd100000 (functAdd100000_out, demultiplexer_3_out0, demultiplexer_4_out4);
  and functSub100010 (functSub100010_out, demultiplexer_3_out2, demultiplexer_4_out4);
  and functMult011000 (functMult011000_out, demultiplexer_3_out0, demultiplexer_4_out3);
  and functDiv011010 (functDiv011010_out, demultiplexer_3_out2, demultiplexer_4_out3);
  and functMflo010010 (functMflo010010_out, demultiplexer_3_out2, demultiplexer_4_out2);
  and functMfhi010000 (functMfhi010000_out, demultiplexer_3_out0, demultiplexer_4_out2);
  and functSll000000 (functSll000000_out, demultiplexer_3_out0, demultiplexer_4_out0);
  and functSrl000010 (functSrl000010_out, demultiplexer_3_out2, demultiplexer_4_out0);
  and functSlt101010 (functSlt101010_out, demultiplexer_3_out2, demultiplexer_4_out5);
  Multiplexer #(.width(32)) multiplexer_2 (.in0({32{1'b0}}), .in1(data), .out(add), .sel(functAdd100000_out));
  Multiplexer #(.width(32)) multiplexer_3 (.in0({32{1'b0}}), .in1(data), .out(sub), .sel(functSub100010_out));
  Multiplexer #(.width(32)) multiplexer_4 (.in0({32{1'b0}}), .in1(data), .out(mult), .sel(functMult011000_out));
  Multiplexer #(.width(32)) multiplexer_5 (.in0({32{1'b0}}), .in1(data), .out(div), .sel(functDiv011010_out));
  Multiplexer #(.width(32)) multiplexer_6 (.in0({32{1'b0}}), .in1(data), .out(mflo), .sel(functMflo010010_out));
  Multiplexer #(.width(32)) multiplexer_7 (.in0({32{1'b0}}), .in1(data), .out(mfhi), .sel(functMfhi010000_out));
  Multiplexer #(.width(32)) multiplexer_8 (.in0({32{1'b0}}), .in1(data), .out(shiftll), .sel(functSll000000_out));
  Multiplexer #(.width(32)) multiplexer_9 (.in0({32{1'b0}}), .in1(data), .out(shiftrl), .sel(functSrl000010_out));
  Multiplexer #(.width(32)) multiplexer_10 (.in0({32{1'b0}}), .in1(data), .out(slt), .sel(functSlt101010_out));

  // Notes on the sheet:
  //   order of demultiplexors
  //   funct code
  //   000
  //   001
  //   010
  //   011
  //   100
  //   101
  //   110
  //   111
  //   opcode
  //   lower order bits
  //   higher order bits
  //   order of demultiplexors
  //   output0 000
  //   output1 001
  //   output2 010
  //   output3 011
  //   output4 100
  //   output5 101
  //   output6 110
  //   output7 111
  //   lower order bits
  //   data
  //   need multiplexor to give which funct code is matching the funct code given
  //   higher order bits
  //   data
endmodule

module addiSubcircuit (
  input  [31:0] in_1,
  output [4:0] rs,
  output [4:0] rt,
  output [4:0] rd,
  output [31:0] imm,
  output reg_write_e,
  output imm_sel,
  output [3:0] ALU_code
);

  assign imm = {{16{1'b0}}, in_1[15:0]};  // Bit_Extender bit_extender_1

  assign ALU_code = 4'b0011;
  assign imm_sel = 1'b1;
  assign rd = in_1[20:16];
  assign reg_write_e = 1'b1;
  assign rs = in_1[25:21];
  assign rt = {5{1'b0}};
endmodule

module mfhiSubcircuit (
  input  [31:0] in_1,
  output [4:0] rs,
  output [4:0] rt,
  output [4:0] rd,
  output [31:0] imm,
  output reg_write_e,
  output imm_sel,
  output [3:0] ALU_code
);


  assign ALU_code = 4'b0110;
  assign imm = {32{1'b0}};
  assign imm_sel = 1'b0;
  assign rd = in_1[20:16];
  assign reg_write_e = 1'b1;
  assign rs = {5{1'b0}};
  assign rt = {5{1'b0}};
endmodule

module norSubcircuit (
  input  [31:0] in_1,
  output [4:0] rs,
  output [4:0] rt,
  output [4:0] rd,
  output [31:0] imm,
  output reg_write_e,
  output imm_sel,
  output [4:0] ALU_code
);


  assign ALU_code = 5'b10101;
  assign imm = {32{1'b0}};
  assign imm_sel = 1'b0;
  assign rd = in_1[15:11];
  assign reg_write_e = 1'b1;
  assign rs = in_1[25:21];
  assign rt = in_1[20:16];
endmodule

module xorSubciruit (
  input  [31:0] in_1,
  output [4:0] rs,
  output [4:0] rt,
  output [4:0] rd,
  output [31:0] imm,
  output reg_write_e,
  output imm_sel,
  output [4:0] ALU_code
);


  assign ALU_code = 5'b10111;
  assign imm = {32{1'b0}};
  assign imm_sel = 1'b0;
  assign rd = in_1[15:11];
  assign reg_write_e = 1'b1;
  assign rs = in_1[25:21];
  assign rt = in_1[20:16];
endmodule
