// Logisim project Project4.circ as structural Verilog: 40 circuits, main circuit regfile
module regfile (
  input  [31:0] rd_data,
  input  [4:0] rt,
  input  [4:0] rd,
  input  [4:0] rs,
  input  write_e,
  output [31:0] rs_data,
  output [31:0] rt_data
);

  wire clock_1_out, clock_2_out, clock_3_out, clock_4_out, clock_5_out, clock_6_out, clock_7_out,
       clock_8_out, clock_9_out, clock_10_out, clock_11_out, clock_12_out, clock_13_out, clock_14_out,
       clock_15_out, clock_16_out, clock_17_out, clock_18_out, clock_19_out, clock_20_out, clock_21_out,
       clock_22_out, clock_23_out, clock_24_out, clock_25_out, clock_26_out, clock_27_out, clock_28_out,
       clock_29_out, clock_30_out, clock_32_out, demultiplexer_2_out1, demultiplexer_2_out2,
       demultiplexer_2_out3, demultiplexer_2_out4, demultiplexer_2_out5, demultiplexer_2_out6,
       demultiplexer_2_out7, demultiplexer_2_out8, demultiplexer_2_out9, demultiplexer_2_out10,
       demultiplexer_2_out11, demultiplexer_2_out12, demultiplexer_2_out13, demultiplexer_2_out14,
       demultiplexer_2_out15, demultiplexer_2_out16, demultiplexer_2_out17, demultiplexer_2_out18,
       demultiplexer_2_out19, demultiplexer_2_out20, demultiplexer_2_out21, demultiplexer_2_out22,
       demultiplexer_2_out23, demultiplexer_2_out24, demultiplexer_2_out25, demultiplexer_2_out26,
       demultiplexer_2_out27, demultiplexer_2_out28, demultiplexer_2_out29, demultiplexer_2_out30,
       demultiplexer_2_out31;
  wire [31:0] demultiplexer_1_out1, demultiplexer_1_out2, demultiplexer_1_out3, demultiplexer_1_out4,
       demultiplexer_1_out5, demultiplexer_1_out6, demultiplexer_1_out7, demultiplexer_1_out8,
       demultiplexer_1_out9, demultiplexer_1_out10, demultiplexer_1_out11, demultiplexer_1_out12,
       demultiplexer_1_out13, demultiplexer_1_out14, demultiplexer_1_out15, demultiplexer_1_out16,
       demultiplexer_1_out17, demultiplexer_1_out18, demultiplexer_1_out19, demultiplexer_1_out20,
       demultiplexer_1_out21, demultiplexer_1_out22, demultiplexer_1_out23, demultiplexer_1_out24,
       demultiplexer_1_out25, demultiplexer_1_out26, demultiplexer_1_out27, demultiplexer_1_out28,
       demultiplexer_1_out29, demultiplexer_1_out30, demultiplexer_1_out31, reg1_q, reg2_q, reg3_q, reg4_q,
       reg5_q, reg6_q, reg7_q, reg8_q, reg9_q, reg10_q, reg11_q, reg12_q, reg13_q, reg14_q, reg15_q, reg16_q,
       reg17_q, reg18_q, reg19_q, reg20_q, reg21_q, reg22_q, reg23_q, reg24_q, reg25_q, reg26_q, reg27_q,
       reg28_q, reg29_q, reg30_q, reg31_q;

  Demultiplexer #(.select(5), .width(32)) demultiplexer_1 (
    .out1(demultiplexer_1_out1), .out2(demultiplexer_1_out2), .out3(demultiplexer_1_out3),
    .out4(demultiplexer_1_out4), .out5(demultiplexer_1_out5), .out6(demultiplexer_1_out6),
    .out7(demultiplexer_1_out7), .out8(demultiplexer_1_out8), .out9(demultiplexer_1_out9),
    .out10(demultiplexer_1_out10), .out11(demultiplexer_1_out11), .out12(demultiplexer_1_out12),
    .out13(demultiplexer_1_out13), .out14(demultiplexer_1_out14), .out15(demultiplexer_1_out15),
    .out16(demultiplexer_1_out16), .out17(demultiplexer_1_out17), .out18(demultiplexer_1_out18),
    .out19(demultiplexer_1_out19), .out20(demultiplexer_1_out20), .out21(demultiplexer_1_out21),
    .out22(demultiplexer_1_out22), .out23(demultiplexer_1_out23), .out24(demultiplexer_1_out24),
    .out25(demultiplexer_1_out25), .out26(demultiplexer_1_out26), .out27(demultiplexer_1_out27),
    .out28(demultiplexer_1_out28), .out29(demultiplexer_1_out29), .out30(demultiplexer_1_out30),
    .out31(demultiplexer_1_out31), .in(rd_data), .sel(rd));  // open: out0
  Demultiplexer #(.select(5)) demultiplexer_2 (
    .out1(demultiplexer_2_out1), .out2(demultiplexer_2_out2), .out3(demultiplexer_2_out3),
    .out4(demultiplexer_2_out4), .out5(demultiplexer_2_out5), .out6(demultiplexer_2_out6),
    .out7(demultiplexer_2_out7), .out8(demultiplexer_2_out8), .out9(demultiplexer_2_out9),
    .out10(demultiplexer_2_out10), .out11(demultiplexer_2_out11), .out12(demultiplexer_2_out12),
    .out13(demultiplexer_2_out13), .out14(demultiplexer_2_out14), .out15(demultiplexer_2_out15),
    .out16(demultiplexer_2_out16), .out17(demultiplexer_2_out17), .out18(demultiplexer_2_out18),
    .out19(demultiplexer_2_out19), .out20(demultiplexer_2_out20), .out21(demultiplexer_2_out21),
    .out22(demultiplexer_2_out22), .out23(demultiplexer_2_out23), .out24(demultiplexer_2_out24),
    .out25(demultiplexer_2_out25), .out26(demultiplexer_2_out26), .out27(demultiplexer_2_out27),
    .out28(demultiplexer_2_out28), .out29(demultiplexer_2_out29), .out30(demultiplexer_2_out30),
    .out31(demultiplexer_2_out31), .in(write_e), .sel(rd));  // open: out0
  Register #(.width(32)) reg1 (
    .D(demultiplexer_1_out1), .en(demultiplexer_2_out1), .clk(clock_1_out), .Q(reg1_q));  // open: clr
  Clock clock_1 (.out(clock_1_out));
  Register #(.width(32)) reg2 (
    .D(demultiplexer_1_out2), .en(demultiplexer_2_out2), .clk(clock_2_out), .Q(reg2_q));  // open: clr
  Clock clock_2 (.out(clock_2_out));
  Register #(.width(32)) reg3 (
    .D(demultiplexer_1_out3), .en(demultiplexer_2_out3), .clk(clock_3_out), .Q(reg3_q));  // open: clr
  Clock clock_3 (.out(clock_3_out));
  Register #(.width(32)) reg4 (
    .D(demultiplexer_1_out4), .en(demultiplexer_2_out4), .clk(clock_4_out), .Q(reg4_q));  // open: clr
  Clock clock_4 (.out(clock_4_out));
  Register #(.width(32)) reg5 (
    .D(demultiplexer_1_out5), .en(demultiplexer_2_out5), .clk(clock_5_out), .Q(reg5_q));  // open: clr
  Clock clock_5 (.out(clock_5_out));
  Clock clock_6 (.out(clock_6_out));
  Register #(.width(32)) reg6 (
    .D(demultiplexer_1_out6), .en(demultiplexer_2_out6), .clk(clock_6_out), .Q(reg6_q));  // open: clr
  Register #(.width(32)) reg7 (
    .D(demultiplexer_1_out7), .en(demultiplexer_2_out7), .clk(clock_7_out), .Q(reg7_q));  // open: clr
  Clock clock_7 (.out(clock_7_out));
  Register #(.width(32)) reg8 (
    .D(demultiplexer_1_out8), .en(demultiplexer_2_out8), .clk(clock_8_out), .Q(reg8_q));  // open: clr
  Clock clock_8 (.out(clock_8_out));
  Register #(.width(32)) reg9 (
    .D(demultiplexer_1_out9), .en(demultiplexer_2_out9), .clk(clock_9_out), .Q(reg9_q));  // open: clr
  Clock clock_9 (.out(clock_9_out));
  Register #(.width(32)) reg10 (
    .D(demultiplexer_1_out10), .en(demultiplexer_2_out10), .clk(clock_10_out), .Q(reg10_q));  // open: clr
  Clock clock_10 (.out(clock_10_out));
  Clock clock_11 (.out(clock_11_out));
  Register #(.width(32)) reg11 (
    .D(demultiplexer_1_out11), .en(demultiplexer_2_out11), .clk(clock_11_out), .Q(reg11_q));  // open: clr
  Register #(.width(32)) reg12 (
    .D(demultiplexer_1_out12), .en(demultiplexer_2_out12), .clk(clock_12_out), .Q(reg12_q));  // open: clr
  Clock clock_12 (.out(clock_12_out));
  Register #(.width(32)) reg13 (
    .D(demultiplexer_1_out13), .en(demultiplexer_2_out13), .clk(clock_13_out), .Q(reg13_q));  // open: clr
  Clock clock_13 (.out(clock_13_out));
  Register #(.width(32)) reg14 (
    .D(demultiplexer_1_out14), .en(demultiplexer_2_out14), .clk(clock_14_out), .Q(reg14_q));  // open: clr
  Clock clock_14 (.out(clock_14_out));
  Clock clock_15 (.out(clock_15_out));
  Register #(.width(32)) reg15 (
    .D(demultiplexer_1_out15), .en(demultiplexer_2_out15), .clk(clock_15_out), .Q(reg15_q));  // open: clr
  Register #(.width(32)) reg16 (
    .D(demultiplexer_1_out16), .en(demultiplexer_2_out16), .clk(clock_16_out), .Q(reg16_q));  // open: clr
  Clock clock_16 (.out(clock_16_out));
  Register #(.width(32)) reg17 (
    .D(demultiplexer_1_out17), .en(demultiplexer_2_out17), .clk(clock_17_out), .Q(reg17_q));  // open: clr
  Clock clock_17 (.out(clock_17_out));
  Register #(.width(32)) reg18 (
    .D(demultiplexer_1_out18), .en(demultiplexer_2_out18), .clk(clock_18_out), .Q(reg18_q));  // open: clr
  Clock clock_18 (.out(clock_18_out));
  Clock clock_19 (.out(clock_19_out));
  Register #(.width(32)) reg19 (
    .D(demultiplexer_1_out19), .en(demultiplexer_2_out19), .clk(clock_19_out), .Q(reg19_q));  // open: clr
  Clock clock_20 (.out(clock_20_out));
  Register #(.width(32)) reg20 (
    .D(demultiplexer_1_out20), .en(demultiplexer_2_out20), .clk(clock_20_out), .Q(reg20_q));  // open: clr
  Register #(.width(32)) reg21 (
    .D(demultiplexer_1_out21), .en(demultiplexer_2_out21), .clk(clock_21_out), .Q(reg21_q));  // open: clr
  Clock clock_21 (.out(clock_21_out));
  Register #(.width(32)) reg22 (
    .D(demultiplexer_1_out22), .en(demultiplexer_2_out22), .clk(clock_22_out), .Q(reg22_q));  // open: clr
  Clock clock_22 (.out(clock_22_out));
  Register #(.width(32)) reg23 (
    .D(demultiplexer_1_out23), .en(demultiplexer_2_out23), .clk(clock_23_out), .Q(reg23_q));  // open: clr
  Clock clock_23 (.out(clock_23_out));
  Clock clock_24 (.out(clock_24_out));
  Register #(.width(32)) reg24 (
    .D(demultiplexer_1_out24), .en(demultiplexer_2_out24), .clk(clock_24_out), .Q(reg24_q));  // open: clr
  Register #(.width(32)) reg25 (
    .D(demultiplexer_1_out25), .en(demultiplexer_2_out25), .clk(clock_25_out), .Q(reg25_q));  // open: clr
  Clock clock_25 (.out(clock_25_out));
  Register #(.width(32)) reg26 (
    .D(demultiplexer_1_out26), .en(demultiplexer_2_out26), .clk(clock_26_out), .Q(reg26_q));  // open: clr
  Clock clock_26 (.out(clock_26_out));
  Register #(.width(32)) reg27 (
    .D(demultiplexer_1_out27), .en(demultiplexer_2_out27), .clk(clock_27_out), .Q(reg27_q));  // open: clr
  Clock clock_27 (.out(clock_27_out));
  Clock clock_28 (.out(clock_28_out));
  Register #(.width(32)) reg28 (
    .D(demultiplexer_1_out28), .en(demultiplexer_2_out28), .clk(clock_28_out), .Q(reg28_q));  // open: clr
  Clock clock_29 (.out(clock_29_out));
  Register #(.width(32)) reg29 (
    .D(demultiplexer_1_out29), .en(demultiplexer_2_out29), .clk(clock_29_out), .Q(reg29_q));  // open: clr
  Register #(.width(32)) reg30 (
    .D(demultiplexer_1_out30), .en(demultiplexer_2_out30), .clk(clock_30_out), .Q(reg30_q));  // open: clr
  Clock clock_30 (.out(clock_30_out));
  Clock clock_31 ();  // open: out
  Register #(.width(32)) reg31 (
    .D(demultiplexer_1_out31), .en(demultiplexer_2_out31), .clk(clock_32_out), .Q(reg31_q));  // open: clr
  Clock clock_32 (.out(clock_32_out));
  Multiplexer #(.select(5), .width(32)) multiplexer_1 (
    .in0({32{1'b0}}), .in1(reg1_q), .in2(reg2_q), .in3(reg3_q), .in4(reg4_q), .in5(reg5_q), .in6(reg6_q),
    .in7(reg7_q), .in8(reg8_q), .in9(reg9_q), .in10(reg10_q), .in11(reg11_q), .in12(reg12_q), .in13(reg13_q),
    .in14(reg14_q), .in15(reg15_q), .in16(reg16_q), .in17(reg17_q), .in18(reg18_q), .in19(reg19_q),
    .in20(reg20_q), .in21(reg21_q), .in22(reg22_q), .in23(reg23_q), .in24(reg24_q), .in25(reg25_q),
    .in26(reg26_q), .in27(reg27_q), .in28(reg28_q), .in29(reg29_q), .in30(reg30_q), .in31(reg31_q),
    .out(rs_data), .sel(rs));
  Multiplexer #(.select(5), .width(32)) multiplexer_2 (
    .in0({32{1'b0}}), .in1(reg1_q), .in2(reg2_q), .in3(reg3_q), .in4(reg4_q), .in5(reg5_q), .in6(reg6_q),
    .in7(reg7_q), .in8(reg8_q), .in9(reg9_q), .in10(reg10_q), .in11(reg11_q), .in12(reg12_q), .in13(reg13_q),
    .in14(reg14_q), .in15(reg15_q), .in16(reg16_q), .in17(reg17_q), .in18(reg18_q), .in19(reg19_q),
    .in20(reg20_q), .in21(reg21_q), .in22(reg22_q), .in23(reg23_q), .in24(reg24_q), .in25(reg25_q),
    .in26(reg26_q), .in27(reg27_q), .in28(reg28_q), .in29(reg29_q), .in30(reg30_q), .in31(reg31_q),
    .out(rt_data), .sel(rt));

  // Notes on the sheet:
  //   rs Multi
  //   rt Multi
endmodule

module ALU (
  input  [31:0] OP1,
  input  [31:0] OP2,
  input  [4:0] ALU_CODE,
  output [31:0] Res,
  output is_equal
);

  wire clock_1_out, clock_2_out, comparator_1_lt, comparator_3_eq, comparator_4_eq, or_2_out;
  wire [4:0] bit_extender_1_out, bit_extender_2_out;
  wire [31:0] adder_1_out, and_1_out, bit_extender_3_out, divider_1_out, divider_1_rem, HI_q, LO_q,
       multiplexer_1_out, multiplexer_2_out, multiplier_1_cout, multiplier_1_out, nor_1_out, or_1_out,
       shifter_1_out, shifter_2_out, subtractor_1_out, undriven, xor_1_out;

  Bit_Extender #(.in_width(32), .out_width(5)) bit_extender_1 (.in(OP2), .out(bit_extender_1_out));
  Bit_Extender #(.in_width(32), .out_width(5)) bit_extender_2 (.in(OP2), .out(bit_extender_2_out));
  assign or_1_out = OP1 | OP2;  // OR_Gate or_1, 32 bits wide
  assign nor_1_out = ~(OP1 | OP2);  // NOR_Gate nor_1, 32 bits wide
  assign xor_1_out = OP1 ^ OP2;  // XOR_Gate xor_1, 32 bits wide
  assign and_1_out = OP2 & OP1;  // AND_Gate and_1, 32 bits wide
  Comparator #(.width(32)) comparator_1 (.a(OP1), .b(OP2), .lt(comparator_1_lt));  // open: gt, eq
  Comparator #(.mode("unsigned"), .width(32)) comparator_2 (.a(OP1), .b(OP2), .eq(is_equal));  // open: gt, lt
  Adder #(.width(32)) adder_1 (.a(OP1), .b(OP2), .out(adder_1_out));  // open: cin, cout
  Subtractor #(.width(32)) subtractor_1 (.a(OP1), .b(OP2), .out(subtractor_1_out));  // open: bin, bout
  Multiplier #(.width(32)) multiplier_1 (
    .a(OP1), .b(OP2), .out(multiplier_1_out), .cout(multiplier_1_cout));  // open: cin
  Divider #(.width(32)) divider_1 (.a(OP1), .b(OP2), .out(divider_1_out), .rem(divider_1_rem));  // open: upper
  Shifter #(.width(32)) shifter_1 (.in(OP1), .\dist (bit_extender_1_out), .out(shifter_1_out));
  Shifter #(.shift("lr"), .width(32)) shifter_2 (.in(OP1), .\dist (bit_extender_2_out), .out(shifter_2_out));
  assign bit_extender_3_out = {{31{comparator_1_lt}}, comparator_1_lt};  // Bit_Extender bit_extender_3
  Multiplexer #(.width(32)) multiplexer_1 (
    .in0(multiplier_1_cout), .in1(divider_1_rem), .out(multiplexer_1_out), .sel(comparator_4_eq));
  Comparator #(.width(5)) comparator_3 (.a(ALU_CODE), .b(5'b00010), .eq(comparator_3_eq));  // open: gt, lt
  Comparator #(.width(5)) comparator_4 (.a(ALU_CODE), .b(5'b00011), .eq(comparator_4_eq));  // open: gt, lt
  Multiplexer #(.width(32)) multiplexer_2 (
    .in0(multiplier_1_out), .in1(divider_1_out), .out(multiplexer_2_out), .sel(comparator_4_eq));
  Multiplexer #(.select(5), .width(32)) multiplexer_3 (
    .in0(adder_1_out), .in1(subtractor_1_out), .in2(multiplier_1_out), .in3(divider_1_out), .in4(LO_q),
    .in5(HI_q), .in6(shifter_1_out), .in7(shifter_2_out), .in8(or_1_out), .in9(undriven), .in10(xor_1_out),
    .in11(and_1_out), .in12(bit_extender_3_out), .out(Res), .sel(ALU_CODE));  // open: in13, in14, in15, in16, in17, in18, in19, in20, in21, in22, in23, in24, in25, in26, in27, in28, in29, in30, in31
  or or_2 (or_2_out, comparator_3_eq, comparator_4_eq);
  Register #(.width(32)) HI (.D(multiplexer_1_out), .en(or_2_out), .clk(clock_1_out), .Q(HI_q));  // open: clr
  Clock clock_1 (.out(clock_1_out));
  Clock clock_2 (.out(clock_2_out));
  Register #(.width(32)) LO (.D(multiplexer_2_out), .en(or_2_out), .clk(clock_2_out), .Q(LO_q));  // open: clr

  // Notes on the sheet:
  //   OP1
  //   OP2
  //   hi
endmodule

module CPUmain (
  input  [31:0] DataFromBus,
  output [25:0] AddressToBus,
  output BusWE,
  output [31:0] DataToBus
);

  wire alu_1_is_equal, and_1_out, and_2_out, clock_1_out, control_1_alu_mem_sel, control_1_imm_sel,
       control_1_is_beq, control_1_is_bne, control_1_is_j, control_1_is_jal_or_jalr, control_1_is_jr_or_jalr,
       control_1_reg_write_e, not_1_out, or_1_out;
  wire [4:0] control_1_alu_code, control_1_rd, control_1_rs, control_1_rt;
  wire [15:0] bit_extender_1_out;
  wire [25:0] bit_extender_3_out, shifter_3_out;
  wire [31:0] adder_1_out, adder_2_out, alu_1_res, bit_extender_2_out, control_1_imm, multiplexer_1_out,
       multiplexer_2_out, multiplexer_3_out, multiplexer_4_out, multiplexer_5_out, multiplexer_6_out,
       ProgramCounter_q, regfile_1_rs_data, rom_1_data, shifter_1_out, shifter_2_out;

  Adder #(.width(32)) adder_1 (.a(ProgramCounter_q), .b(32'h4), .out(adder_1_out));  // open: cin, cout
  Shifter #(.width(32)) shifter_1 (.in(control_1_imm), .\dist (5'b00010), .out(shifter_1_out));
  Shifter #(.shift("lr"), .width(32)) shifter_2 (.in(ProgramCounter_q), .\dist (5'b00010), .out(shifter_2_out));
  Adder #(.width(32)) adder_2 (.a(adder_1_out), .b(shifter_1_out), .out(adder_2_out));  // open: cin, cout
  Shifter #(.width(26)) shifter_3 (.in(bit_extender_3_out), .\dist (5'b00010), .out(shifter_3_out));
  or or_1 (or_1_out, and_1_out, and_2_out);
  Bit_Extender #(.in_width(32)) bit_extender_1 (.in(shifter_2_out), .out(bit_extender_1_out));
  Multiplexer #(.width(32)) multiplexer_1 (
    .in0(adder_1_out), .in1(adder_2_out), .out(multiplexer_1_out), .sel(or_1_out));
  assign bit_extender_2_out = {{6{shifter_3_out[25]}}, shifter_3_out};  // Bit_Extender bit_extender_2
  Multiplexer #(.width(32)) multiplexer_2 (
    .in0(bit_extender_2_out), .in1(regfile_1_rs_data), .out(multiplexer_2_out), .sel(control_1_is_jr_or_jalr));
  Register #(.width(32)) ProgramCounter (
    .D(multiplexer_3_out), .en(1'b1), .clk(clock_1_out), .Q(ProgramCounter_q));  // open: clr
  Multiplexer #(.width(32)) multiplexer_3 (
    .in0(multiplexer_1_out), .in1(multiplexer_2_out), .out(multiplexer_3_out), .sel(control_1_is_j));
  Clock clock_1 (.out(clock_1_out));
  ROM #(.addrWidth(16), .dataWidth(32)) rom_1 (.addr(bit_extender_1_out), .data(rom_1_data));
  and and_1 (and_1_out, control_1_is_bne, not_1_out);
  and and_2 (and_2_out, alu_1_is_equal, control_1_is_beq);
  not not_1 (not_1_out, alu_1_is_equal);
  Bit_Extender #(.in_width(32), .out_width(26)) bit_extender_3 (.in(rom_1_data), .out(bit_extender_3_out));
  Multiplexer #(.width(32)) multiplexer_4 (
    .in0(alu_1_res), .in1(DataFromBus), .out(multiplexer_4_out), .sel(control_1_alu_mem_sel));
  Multiplexer #(.width(32)) multiplexer_5 (
    .in0(multiplexer_4_out), .in1(adder_1_out), .out(multiplexer_5_out), .sel(control_1_is_jal_or_jalr));
  regfile regfile_1 (
    .rd_data(multiplexer_5_out), .rd(control_1_rd), .write_e(control_1_reg_write_e), .rs(control_1_rs),
    .rt(control_1_rt), .rs_data(regfile_1_rs_data), .rt_data(DataToBus));
  Control control_1 (
    .Inst(rom_1_data), .rd(control_1_rd), .rt(control_1_rt), .rs(control_1_rs), .imm(control_1_imm),
    .reg_write_e(control_1_reg_write_e), .imm_sel(control_1_imm_sel), .ALU_code(control_1_alu_code),
    .is_beq(control_1_is_beq), .is_bne(control_1_is_bne), .is_j(control_1_is_j),
    .is_jal_or_jalr(control_1_is_jal_or_jalr), .is_jr_or_jalr(control_1_is_jr_or_jalr), .WE_mem(BusWE),
    .ALU_mem_sel(control_1_alu_mem_sel));
  Multiplexer #(.width(32)) multiplexer_6 (
    .in0(DataToBus), .in1(control_1_imm), .out(multiplexer_6_out), .sel(control_1_imm_sel));
  ALU alu_1 (
    .ALU_CODE(control_1_alu_code), .OP1(regfile_1_rs_data), .OP2(multiplexer_6_out), .Res(alu_1_res),
    .is_equal(alu_1_is_equal));
  Shifter #(.shift("lr"), .width(32)) shifter_4 (.\dist (5'b00010));  // open: in, out
  Bit_Extender #(.in_width(32), .out_width(26)) bit_extender_4 (.in(alu_1_res), .out(AddressToBus));

  // Notes on the sheet:
  //   Offset
  //   PC + 4
  //   label for j and jal (word address)
  //   branches
  //   PC + 4 + Offset
  //   jr/jalr
  //   register for jr and jalr
  //   jr/jalr
  //   any j
  //   contents of rom_1 (hex, n*v repeats v):
  //   104000f3 201b0001 105b000d 201b0005 105b0031 201b0009 105b00b1 201b000a 105b00b7 201b000b 105b00b6
  //   201b000c 105b00b6 201b000d 105b00c3 80000c0 23bdfff0 afa80000 afa90004 afaa0008 afab000c 200b0000
  //   80502a 804020 11400005 2008002d ac08ff00 2008ffff 880018 4012 8502a 1140000a 11000009 2009000a
  //   109001a 4810 21290030 216b0001 23bdfffc afa90000 4012 800001e 11600005 216bffff 8fa90000 ac09ff00
  //   23bd0004 800002a 8fa80000 8fa90004 8faa0008 8fab000c 23bd0010 3400008 23bdffb4 afa80000 afa90004
  //   afaa0008 afab000c afac0010 afad0014 afae0018 afaf001c afb00020 afb10024 afb20028 afb3002c afb40030
  //   afb50034 afb60038 afb7003c afa30040 afa00044 20080030 20090031 200a0032 200b0033 200c0034 200d0035
  //   200e0036 200f0037 20100038 20110039 2012002d 20130000 20140000 20150000 2016000a 20170000 20020000
  //   20030000 8c13ff10 12600043 8c13ff14 ac00ff10 20140001 1272000b 1268000c 12690010 126a0014 126b0018
  //   126c001c 126d0020 126e0024 126f0028 1271002c 12720030 80000a3 2014ffff 8000061 20130000 560018 1012
  //   531020 8000061 20130001 560018 1012 531020 8000061 20130002 560018 1012 531020 8000061 20130003
  //   560018 1012 531020 8000061 20130004 560018 1012 531020 8000061 20130005 560018 1012 531020 8000061
  //   20130006 560018 1012 531020 8000061 20130007 560018 1012 531020 8000061 20130008 560018 1012 531020
  //   8000061 20130009 560018 1012 531020 8000061 8c13ff10 1260ffbb 80000a0 8fa80000 8fa90004 8faa0008
  //   8fab000c 8fac0010 8fad0014 8fae0018 8faf001c 8fb00020 8fb10024 8fb20028 8fb3002c 8fb40030 8fb50034
  //   8fb60038 8fb7003c 8fa30040 23bd0044 540018 1012 3400008 23bdfffc afa80000 8c02f004 444020 ac08f004
  //   8fa80000 23bd0004 3400008 80000c0 ac04ff00 3400008 23bdfff8 afba0000 afbb0004 8c1bff10 13600003
  //   8c02ff14 ac00ff10 80000ce 8c1bff10 1760fffb 80000cb 8fba0000 8fbb0004 23bd0008 3400008 23bdffec
  //   afa80000 afa90004 afaa0008 afab000c afa40010 200b0064 ac0bff04 ac0bff2c ac0bff38 ac0aff08 ac0aff1c
  //   ac0aff34 20420000 20420000 8c890000 200b0001 112b0009 200a0001 ac09ff0c ac09ff18 ac09ff30 20840004
  //   80000df ac0aff08 ac0aff1c ac0aff34 8fa80000 8fa90004 8faa0008 8fab000c 8fa40010 23bd0014 3400008
  //   20420000 20420000 20020000 201df000 ac02f004 23bdffd0 200800ff 84a00 85400 200b007f b6200 b6c00
  //   afaa0000 14cc020 afb80004 149c020 afb80008 1a9c020 afb8000c afa90010 169c020 afb80014 109c020
  //   afb80018 10cc020 afb8001c afa80020 10dc020 afb80024 10ac020 afb80028 16ac020 afb8002c 20100080
  //   2011007e 20120040 2013003f 20140001 20150000 2110018 4012 84080 82020 20020009 d00c 40b020 20170000
  //   20180061 8c08ff10 11000004 2002000c d00c 407820 ac00ff10 20090061 15e90004 12400015 2014ffff
  //   20150000 8000142 20090064 15e90004 1250000f 20140001 20150000 8000142 20090073 15e90004 12710009
  //   20140000 20150001 8000142 20090077 15e90004 12600003 20140000 2015ffff 8000142 2549020 2759820
  //   2700018 4012 1124020 84080 1164020 8d090000 200a0001 112a0015 ad0a0000 240402a 15000012 212402a
  //   15000010 260402a 1500000e 233402a 1500000c 22f70001 2009000c 2e9001a b810 174880 13d4820 8d290000
  //   ac12ff20 ac13ff24 ac09ff28 ac00ff2c 8000124 2002000b 20040059 d00c 2004004f d00c 20040055 d00c
  //   20040020 d00c 2004004c d00c 2004004f d00c 20040053 d00c 20040045 d00c 20040020 d00c 2004003c d00c
  //   20040033 d00c 2002000a d00c
  //   1 if two registers are ==
  //   PC + 4
  //   ALU
  //   MEM
  //   jal/jalr
  //   attach to data in
  //   attach to is_jal_OR_jal
  //   attach to is_beq
  //   attach to is_jr
  //   attach to is_bne
  //   attach to ALU_memselect
  //   attach to is_j
  //   connect to equal
  //   attach to we_mem
  //   addr
  //   we
  //   data
  //   data_in
endmodule

module sixBitDemultiplexer (
  input  [31:0] data,
  output [31:0] add,
  output [31:0] sub,
  output [31:0] mult,
  output [31:0] div,
  output [31:0] mflo,
  output [31:0] mfhi,
  output [31:0] shiftll,
  output [31:0] shiftrl,
  output [31:0] slt,
  output [31:0] andOutput,
  output [31:0] orOutput,
  output [31:0] norOutput,
  output [31:0] xorOutput,
  output [31:0] addi,
  output [31:0] jrOutput,
  output [31:0] jalrOutput,
  output [31:0] syscallOutput,
  output [31:0] lwOutput,
  output [31:0] swOutput,
  output [31:0] beqOutput,
  output [31:0] bneOutput,
  output [31:0] jOutput,
  output [31:0] jalOutput
);

  wire demultiplexer_1_out0, demultiplexer_1_out2, demultiplexer_1_out3, demultiplexer_1_out4,
       demultiplexer_1_out5, demultiplexer_2_out0, demultiplexer_2_out1, demultiplexer_2_out4,
       demultiplexer_2_out5, demultiplexer_3_out0, demultiplexer_3_out1, demultiplexer_3_out2,
       demultiplexer_3_out4, demultiplexer_3_out5, demultiplexer_3_out6, demultiplexer_3_out7,
       demultiplexer_4_out0, demultiplexer_4_out1, demultiplexer_4_out2, demultiplexer_4_out3,
       demultiplexer_4_out4, demultiplexer_4_out5, functAdd100000_out, functAND100100_out,
       functDiv011010_out, functionJALR001001_out, functionJR001000_out, functionSyscal001100_out,
       functMfhi010000_out, functMflo010010_out, functMult011000_out, functNOR100111_out, functOR100101_out,
       functSll000000_out, functSlt101010_out, functSrl000010_out, functSub100010_out, functXOR100110_out,
       opcode000000_out, opcode000010_out, opcode000011_out, opcode000100_out, opcode000101_out,
       opcode001000_out, opcode100011_out, opcode101011_out;

  Demultiplexer #(.select(3)) demultiplexer_1 (
    .out0(demultiplexer_1_out0), .out2(demultiplexer_1_out2), .out3(demultiplexer_1_out3),
    .out4(demultiplexer_1_out4), .out5(demultiplexer_1_out5), .in(1'b1), .sel(data[28:26]));  // open: out1, out6, out7
  Demultiplexer #(.select(3)) demultiplexer_2 (
    .out0(demultiplexer_2_out0), .out1(demultiplexer_2_out1), .out4(demultiplexer_2_out4),
    .out5(demultiplexer_2_out5), .in(1'b1), .sel(data[31:29]));  // open: out2, out3, out6, out7
  and opcode000000 (opcode000000_out, demultiplexer_1_out0, demultiplexer_2_out0);
  and opcode001000 (opcode001000_out, demultiplexer_2_out1, demultiplexer_1_out0);
  and opcode100011 (opcode100011_out, demultiplexer_1_out3, demultiplexer_2_out4);
  and opcode101011 (opcode101011_out, demultiplexer_1_out3, demultiplexer_2_out5);
  and opcode000100 (opcode000100_out, demultiplexer_1_out4, demultiplexer_2_out0);
  and opcode000101 (opcode000101_out, demultiplexer_1_out5, demultiplexer_2_out0);
  and opcode000010 (opcode000010_out, demultiplexer_1_out2, demultiplexer_2_out0);
  and opcode000011 (opcode000011_out, demultiplexer_1_out3, demultiplexer_2_out0);
  Demultiplexer #(.select(3)) demultiplexer_3 (
    .out0(demultiplexer_3_out0), .out1(demultiplexer_3_out1), .out2(demultiplexer_3_out2),
    .out4(demultiplexer_3_out4), .out5(demultiplexer_3_out5), .out6(demultiplexer_3_out6),
    .out7(demultiplexer_3_out7), .in(opcode000000_out), .sel(data[2:0]));  // open: out3
  Demultiplexer #(.select(3)) demultiplexer_4 (
    .out0(demultiplexer_4_out0), .out1(demultiplexer_4_out1), .out2(demultiplexer_4_out2),
    .out3(demultiplexer_4_out3), .out4(demultiplexer_4_out4), .out5(demultiplexer_4_out5),
    .in(opcode000000_out), .sel(data[5:3]));  // open: out6, out7
  Multiplexer #(.width(32)) multiplexer_1 (.in0({32{1'b0}}), .in1(data), .out(addi), .sel(opcode001000_out));
  Multiplexer #(.width(32)) multiplexer_2 (.in0({32{1'b0}}), .in1(data), .out(lwOutput), .sel(opcode100011_out));
  Multiplexer #(.width(32)) multiplexer_3 (.in0({32{1'b0}}), .in1(data), .out(swOutput), .sel(opcode101011_out));
  Multiplexer #(.width(32)) multiplexer_4 (.in0({32{1'b0}}), .in1(data), .out(beqOutput), .sel(opcode000100_out));
  Multiplexer #(.width(32)) multiplexer_5 (.in0({32{1'b0}}), .in1(data), .out(bneOutput), .sel(opcode000101_out));
  Multiplexer #(.width(32)) multiplexer_6 (.in0({32{1'b0}}), .in1(data), .out(jOutput), .sel(opcode000010_out));
  Multiplexer #(.width(32)) multiplexer_7 (.in0({32{1'b0}}), .in1(data), .out(jalOutput), .sel(opcode000011_out));
  and functAdd100000 (functAdd100000_out, demultiplexer_3_out0, demultiplexer_4_out4);
  and functSub100010 (functSub100010_out, demultiplexer_3_out2, demultiplexer_4_out4);
  and functMult011000 (functMult011000_out, demultiplexer_3_out0, demultiplexer_4_out3);
  and functDiv011010 (functDiv011010_out, demultiplexer_3_out2, demultiplexer_4_out3);
  and functMflo010010 (functMflo010010_out, demultiplexer_3_out2, demultiplexer_4_out2);
  and functMfhi010000 (functMfhi010000_out, demultiplexer_3_out0, demultiplexer_4_out2);
  and functSll000000 (functSll000000_out, demultiplexer_3_out0, demultiplexer_4_out0);
  and functSrl000010 (functSrl000010_out, demultiplexer_3_out2, demultiplexer_4_out0);
  and functSlt101010 (functSlt101010_out, demultiplexer_3_out2, demultiplexer_4_out5);
  and functAND100100 (functAND100100_out, demultiplexer_4_out4, demultiplexer_3_out4);
  and functOR100101 (functOR100101_out, demultiplexer_4_out4, demultiplexer_3_out5);
  and functNOR100111 (functNOR100111_out, demultiplexer_4_out4, demultiplexer_3_out7);
  and functXOR100110 (functXOR100110_out, demultiplexer_4_out4, demultiplexer_3_out6);
  and functionJR001000 (functionJR001000_out, demultiplexer_3_out0, demultiplexer_4_out1);
  and functionJALR001001 (functionJALR001001_out, demultiplexer_3_out1, demultiplexer_4_out1);
  and functionSyscal001100 (functionSyscal001100_out, demultiplexer_3_out4, demultiplexer_4_out1);
  Multiplexer #(.width(32)) multiplexer_8 (.in0({32{1'b0}}), .in1(data), .out(add), .sel(functAdd100000_out));
  Multiplexer #(.width(32)) multiplexer_9 (.in0({32{1'b0}}), .in1(data), .out(sub), .sel(functSub100010_out));
  Multiplexer #(.width(32)) multiplexer_10 (.in0({32{1'b0}}), .in1(data), .out(mult), .sel(functMult011000_out));
  Multiplexer #(.width(32)) multiplexer_11 (.in0({32{1'b0}}), .in1(data), .out(div), .sel(functDiv011010_out));
  Multiplexer #(.width(32)) multiplexer_12 (.in0({32{1'b0}}), .in1(data), .out(mflo), .sel(functMflo010010_out));
  Multiplexer #(.width(32)) multiplexer_13 (.in0({32{1'b0}}), .in1(data), .out(mfhi), .sel(functMfhi010000_out));
  Multiplexer #(.width(32)) multiplexer_14 (.in0({32{1'b0}}), .in1(data), .out(shiftll), .sel(functSll000000_out));
  Multiplexer #(.width(32)) multiplexer_15 (.in0({32{1'b0}}), .in1(data), .out(shiftrl), .sel(functSrl000010_out));
  Multiplexer #(.width(32)) multiplexer_16 (.in0({32{1'b0}}), .in1(data), .out(slt), .sel(functSlt101010_out));
  Multiplexer #(.width(32)) multiplexer_17 (.in0({32{1'b0}}), .in1(data), .out(andOutput), .sel(functAND100100_out));
  Multiplexer #(.width(32)) multiplexer_18 (.in0({32{1'b0}}), .in1(data), .out(orOutput), .sel(functOR100101_out));
  Multiplexer #(.width(32)) multiplexer_19 (.in0({32{1'b0}}), .in1(data), .out(norOutput), .sel(functNOR100111_out));
  Multiplexer #(.width(32)) multiplexer_20 (.in0({32{1'b0}}), .in1(data), .out(xorOutput), .sel(functXOR100110_out));
  Multiplexer #(.width(32)) multiplexer_21 (.in0({32{1'b0}}), .in1(data), .out(jrOutput), .sel(functionJR001000_out));
  Multiplexer #(.width(32)) multiplexer_22 (
    .in0({32{1'b0}}), .in1(data), .out(jalrOutput), .sel(functionJALR001001_out));
  Multiplexer #(.width(32)) multiplexer_23 (
    .in0({32{1'b0}}), .in1(data), .out(syscallOutput), .sel(functionSyscal001100_out));

  // Notes on the sheet:
  //   output0 000
  //   output1 001
  //   output2 010
  //   output3 011
  //   output4 100
  //   output5 101
  //   output6 110
  //   output7 111
  //   funct code
  //   opcode
  //   order of demultiplexers
  //   000
  //   001
  //   010
  //   011
  //   100
  //   101
  //   110
  //   111
  //   lower order bits
  //   higher order bits
  //   order of demultiplexers
  //   output0 000
  //   output1 001
  //   output2 010
  //   output3 011
  //   output4 100
  //   output5 101
  //   output6 110
  //   output7 111
  //   data
  //   lower order bits
  //   higher order bits
  //   data
endmodule

module TESTminiRegFile (
  input  [4:0] rs,
  input  [4:0] rt,
  input  [4:0] rd,
  input  WE,
  input  [31:0] rdData,
  output [31:0] rsData
);

  wire [31:0] reg1_q, reg2_q, reg3_q, reg4_q;

  Register #(.width(32)) reg1 (.Q(reg1_q));  // open: D, en, clk, clr
  Register #(.width(32)) reg2 (.Q(reg2_q));  // open: D, en, clk, clr
  Register #(.width(32)) reg3 (.Q(reg3_q));  // open: D, en, clk, clr
  Register #(.width(32)) reg4 (.Q(reg4_q));  // open: D, en, clk, clr
  Multiplexer #(.select(5), .width(32)) multiplexer_1 (
    .in0({32{1'b0}}), .in1(reg1_q), .in2(reg2_q), .in3(reg3_q), .in4(reg4_q), .sel(rs));  // open: in5, in6, in7, in8, in9, in10, in11, in12, in13, in14, in15, in16, in17, in18, in19, in20, in21, in22, in23, in24, in25, in26, in27, in28, in29, in30, in31, out
endmodule

module Control (
  input  [31:0] Inst,
  output [4:0] rd,
  output [4:0] rt,
  output [4:0] rs,
  output [31:0] imm,
  output reg_write_e,
  output imm_sel,
  output [4:0] ALU_code,
  output is_beq,
  output is_bne,
  output is_j,
  output is_jal_or_jalr,
  output is_jr_or_jalr,
  output WE_mem,
  output ALU_mem_sel
);

  wire addcontrol_1_imm_sel, addcontrol_1_reg_write_e, addicontrol_1_imm_sel, addicontrol_1_reg_write_e,
       andcontrol_1_imm_sel, andcontrol_1_reg_write_e, beqcontrol_1_imm_sel, beqcontrol_1_is_beq,
       beqcontrol_1_reg_write_e, bnecontrol_1_imm_sel, bnecontrol_1_is_bne, bnecontrol_1_reg_write_e,
       divcontrol_1_imm_sel, divcontrol_1_reg_write_e, jalcontrol_1_is_j, jalcontrol_1_is_jal_or_jalr,
       jalcontrol_1_reg_write_e, jalrcontrol_1_imm_sel, jalrcontrol_1_is_j, jalrcontrol_1_is_jal_or_jalr,
       jalrcontrol_1_is_jr_or_jalr, jalrcontrol_1_reg_write_e, jcontrol_1_is_j, jrcontrol_1_imm_sel,
       jrcontrol_1_is_j, jrcontrol_1_is_jr_or_jalr, jrcontrol_1_reg_write_e, lwcontrol_1_alu_mem_sel,
       lwcontrol_1_imm_sel, lwcontrol_1_reg_write_e, mfhicontrol_1_imm_sel, mfhicontrol_1_reg_write_e,
       mflocontrol_1_imm_sel, mflocontrol_1_reg_write_e, multcontrol_1_imm_sel, multcontrol_1_reg_write_e,
       norcontrol_1_imm_sel, norcontrol_1_reg_write_e, orcontrol_1_imm_sel, orcontrol_1_reg_write_e,
       sllcontrol_1_imm_sel, sllcontrol_1_reg_write_e, sltcontrol_1_imm_sel, sltcontrol_1_reg_write_e,
       srlcontrol_1_imm_sel, srlcontrol_1_reg_write_e, subcontrol_1_imm_sel, subcontrol_1_reg_write_e,
       swcontrol_1_imm_sel, swcontrol_1_reg_write_e, swcontrol_1_we_mem, syscallcontrol_1_imm_sel,
       syscallcontrol_1_is_j, syscallcontrol_1_is_jal_or_jalr, syscallcontrol_1_is_jr_or_jalr,
       syscallcontrol_1_reg_write_e, xorcontrol_1_imm_sel, xorcontrol_1_reg_write_e;
  wire [4:0] addcontrol_1_alu_code, addcontrol_1_rd, addcontrol_1_rs, addcontrol_1_rt,
       addicontrol_1_alu_code, addicontrol_1_rd, addicontrol_1_rs, addicontrol_1_rt, andcontrol_1_alu_code,
       andcontrol_1_rd, andcontrol_1_rs, andcontrol_1_rt, beqcontrol_1_alu_code, beqcontrol_1_rd,
       beqcontrol_1_rs, beqcontrol_1_rt, bnecontrol_1_alu_code, bnecontrol_1_rd, bnecontrol_1_rs,
       bnecontrol_1_rt, divcontrol_1_alu_code, divcontrol_1_rd, divcontrol_1_rs, divcontrol_1_rt,
       jalcontrol_1_rd, jalrcontrol_1_alu_code, jalrcontrol_1_rd, jalrcontrol_1_rs, jalrcontrol_1_rt,
       jrcontrol_1_alu_code, jrcontrol_1_rd, jrcontrol_1_rs, jrcontrol_1_rt, lwcontrol_1_alu_code,
       lwcontrol_1_rd, lwcontrol_1_rs, lwcontrol_1_rt, mfhicontrol_1_alu_code, mfhicontrol_1_rd,
       mfhicontrol_1_rs, mfhicontrol_1_rt, mflocontrol_1_alu_code, mflocontrol_1_rd, mflocontrol_1_rs,
       mflocontrol_1_rt, multcontrol_1_alu_code, multcontrol_1_rd, multcontrol_1_rs, multcontrol_1_rt,
       norcontrol_1_alu_code, norcontrol_1_rd, norcontrol_1_rs, norcontrol_1_rt, orcontrol_1_alu_code,
       orcontrol_1_rd, orcontrol_1_rs, orcontrol_1_rt, sllcontrol_1_alu_code, sllcontrol_1_rd,
       sllcontrol_1_rs, sllcontrol_1_rt, sltcontrol_1_alu_code, sltcontrol_1_rd, sltcontrol_1_rs,
       sltcontrol_1_rt, srlcontrol_1_alu_code, srlcontrol_1_rd, srlcontrol_1_rs, srlcontrol_1_rt,
       subcontrol_1_alu_code, subcontrol_1_rd, subcontrol_1_rs, subcontrol_1_rt, swcontrol_1_alu_code,
       swcontrol_1_rd, swcontrol_1_rs, swcontrol_1_rt, syscallcontrol_1_alu_code, syscallcontrol_1_rd,
       syscallcontrol_1_rs, syscallcontrol_1_rt, xorcontrol_1_alu_code, xorcontrol_1_rd, xorcontrol_1_rs,
       xorcontrol_1_rt;
  wire [31:0] addcontrol_1_imm, addicontrol_1_imm, andcontrol_1_imm, beqcontrol_1_imm, bnecontrol_1_imm,
       divcontrol_1_imm, jalcontrol_1_imm, jalrcontrol_1_imm, jcontrol_1_imm, jrcontrol_1_imm,
       lwcontrol_1_imm, mfhicontrol_1_imm, mflocontrol_1_imm, multcontrol_1_imm, norcontrol_1_imm,
       orcontrol_1_imm, sixbitdemultiplexer_1_add, sixbitdemultiplexer_1_addi,
       sixbitdemultiplexer_1_andoutput, sixbitdemultiplexer_1_beqoutput, sixbitdemultiplexer_1_bneoutput,
       sixbitdemultiplexer_1_div, sixbitdemultiplexer_1_jaloutput, sixbitdemultiplexer_1_jalroutput,
       sixbitdemultiplexer_1_joutput, sixbitdemultiplexer_1_jroutput, sixbitdemultiplexer_1_lwoutput,
       sixbitdemultiplexer_1_mfhi, sixbitdemultiplexer_1_mflo, sixbitdemultiplexer_1_mult,
       sixbitdemultiplexer_1_noroutput, sixbitdemultiplexer_1_oroutput, sixbitdemultiplexer_1_shiftll,
       sixbitdemultiplexer_1_shiftrl, sixbitdemultiplexer_1_slt, sixbitdemultiplexer_1_sub,
       sixbitdemultiplexer_1_swoutput, sixbitdemultiplexer_1_syscalloutput, sixbitdemultiplexer_1_xoroutput,
       sllcontrol_1_imm, sltcontrol_1_imm, srlcontrol_1_imm, subcontrol_1_imm, swcontrol_1_imm,
       syscallcontrol_1_imm, xorcontrol_1_imm;

  sixBitDemultiplexer sixbitdemultiplexer_1 (
    .data(Inst), .add(sixbitdemultiplexer_1_add), .sub(sixbitdemultiplexer_1_sub),
    .mult(sixbitdemultiplexer_1_mult), .div(sixbitdemultiplexer_1_div), .mflo(sixbitdemultiplexer_1_mflo),
    .mfhi(sixbitdemultiplexer_1_mfhi), .shiftll(sixbitdemultiplexer_1_shiftll),
    .shiftrl(sixbitdemultiplexer_1_shiftrl), .slt(sixbitdemultiplexer_1_slt),
    .andOutput(sixbitdemultiplexer_1_andoutput), .orOutput(sixbitdemultiplexer_1_oroutput),
    .norOutput(sixbitdemultiplexer_1_noroutput), .xorOutput(sixbitdemultiplexer_1_xoroutput),
    .addi(sixbitdemultiplexer_1_addi), .jrOutput(sixbitdemultiplexer_1_jroutput),
    .jalrOutput(sixbitdemultiplexer_1_jalroutput), .syscallOutput(sixbitdemultiplexer_1_syscalloutput),
    .lwOutput(sixbitdemultiplexer_1_lwoutput), .swOutput(sixbitdemultiplexer_1_swoutput),
    .beqOutput(sixbitdemultiplexer_1_beqoutput), .bneOutput(sixbitdemultiplexer_1_bneoutput),
    .jOutput(sixbitdemultiplexer_1_joutput), .jalOutput(sixbitdemultiplexer_1_jaloutput));
  addControl addcontrol_1 (
    .data(sixbitdemultiplexer_1_add), .rd(addcontrol_1_rd), .rt(addcontrol_1_rt), .rs(addcontrol_1_rs),
    .imm(addcontrol_1_imm), .reg_write_e(addcontrol_1_reg_write_e), .imm_sel(addcontrol_1_imm_sel),
    .ALU_code(addcontrol_1_alu_code));
  subControl subcontrol_1 (
    .data(sixbitdemultiplexer_1_sub), .rd(subcontrol_1_rd), .rt(subcontrol_1_rt), .rs(subcontrol_1_rs),
    .imm(subcontrol_1_imm), .reg_write_e(subcontrol_1_reg_write_e), .imm_sel(subcontrol_1_imm_sel),
    .ALU_code(subcontrol_1_alu_code));
  multControl multcontrol_1 (
    .data(sixbitdemultiplexer_1_mult), .rd(multcontrol_1_rd), .rt(multcontrol_1_rt), .rs(multcontrol_1_rs),
    .imm(multcontrol_1_imm), .reg_write_e(multcontrol_1_reg_write_e), .imm_sel(multcontrol_1_imm_sel),
    .ALU_code(multcontrol_1_alu_code));
  divControl divcontrol_1 (
    .data(sixbitdemultiplexer_1_div), .rd(divcontrol_1_rd), .rt(divcontrol_1_rt), .rs(divcontrol_1_rs),
    .imm(divcontrol_1_imm), .reg_write_e(divcontrol_1_reg_write_e), .imm_sel(divcontrol_1_imm_sel),
    .ALU_code(divcontrol_1_alu_code));
  mfloControl mflocontrol_1 (
    .data(sixbitdemultiplexer_1_mflo), .rd(mflocontrol_1_rd), .rt(mflocontrol_1_rt), .rs(mflocontrol_1_rs),
    .imm(mflocontrol_1_imm), .reg_write_e(mflocontrol_1_reg_write_e), .imm_sel(mflocontrol_1_imm_sel),
    .ALU_code(mflocontrol_1_alu_code));
  mfhiControl mfhicontrol_1 (
    .in_1(sixbitdemultiplexer_1_mfhi), .rs(mfhicontrol_1_rs), .rt(mfhicontrol_1_rt), .rd(mfhicontrol_1_rd),
    .imm(mfhicontrol_1_imm), .reg_write_e(mfhicontrol_1_reg_write_e), .imm_sel(mfhicontrol_1_imm_sel),
    .ALU_code(mfhicontrol_1_alu_code));
  sllControl sllcontrol_1 (
    .data(sixbitdemultiplexer_1_shiftll), .imm(sllcontrol_1_imm), .rd(sllcontrol_1_rd), .rt(sllcontrol_1_rt),
    .rs(sllcontrol_1_rs), .reg_write_e(sllcontrol_1_reg_write_e), .imm_sel(sllcontrol_1_imm_sel),
    .ALU_code(sllcontrol_1_alu_code));
  srlControl srlcontrol_1 (
    .data(sixbitdemultiplexer_1_shiftrl), .imm(srlcontrol_1_imm), .rd(srlcontrol_1_rd), .rt(srlcontrol_1_rt),
    .rs(srlcontrol_1_rs), .reg_write_e(srlcontrol_1_reg_write_e), .imm_sel(srlcontrol_1_imm_sel),
    .ALU_code(srlcontrol_1_alu_code));
  sltControl sltcontrol_1 (
    .data(sixbitdemultiplexer_1_slt), .rd(sltcontrol_1_rd), .rt(sltcontrol_1_rt), .rs(sltcontrol_1_rs),
    .imm(sltcontrol_1_imm), .reg_write_e(sltcontrol_1_reg_write_e), .imm_sel(sltcontrol_1_imm_sel),
    .ALU_code(sltcontrol_1_alu_code));
  andControl andcontrol_1 (
    .data(sixbitdemultiplexer_1_andoutput), .rd(andcontrol_1_rd), .rt(andcontrol_1_rt), .rs(andcontrol_1_rs),
    .imm(andcontrol_1_imm), .reg_write_e(andcontrol_1_reg_write_e), .imm_sel(andcontrol_1_imm_sel),
    .ALU_code(andcontrol_1_alu_code));
  orControl orcontrol_1 (
    .data(sixbitdemultiplexer_1_oroutput), .rd(orcontrol_1_rd), .rt(orcontrol_1_rt), .rs(orcontrol_1_rs),
    .imm(orcontrol_1_imm), .reg_write_e(orcontrol_1_reg_write_e), .imm_sel(orcontrol_1_imm_sel),
    .ALU_code(orcontrol_1_alu_code));
  xorControl xorcontrol_1 (
    .data(sixbitdemultiplexer_1_xoroutput), .rd(xorcontrol_1_rd), .rt(xorcontrol_1_rt), .rs(xorcontrol_1_rs),
    .imm(xorcontrol_1_imm), .reg_write_e(xorcontrol_1_reg_write_e), .imm_sel(xorcontrol_1_imm_sel),
    .ALU_code(xorcontrol_1_alu_code));
  norControl norcontrol_1 (
    .data(sixbitdemultiplexer_1_noroutput), .rd(norcontrol_1_rd), .rt(norcontrol_1_rt), .rs(norcontrol_1_rs),
    .imm(norcontrol_1_imm), .reg_write_e(norcontrol_1_reg_write_e), .imm_sel(norcontrol_1_imm_sel),
    .ALU_code(norcontrol_1_alu_code));
  addiControl addicontrol_1 (
    .in_1(sixbitdemultiplexer_1_addi), .rs(addicontrol_1_rs), .rt(addicontrol_1_rt), .rd(addicontrol_1_rd),
    .imm(addicontrol_1_imm), .reg_write_e(addicontrol_1_reg_write_e), .imm_sel(addicontrol_1_imm_sel),
    .ALU_code(addicontrol_1_alu_code));
  jrControl jrcontrol_1 (
    .data(sixbitdemultiplexer_1_jroutput), .rd(jrcontrol_1_rd), .rt(jrcontrol_1_rt), .rs(jrcontrol_1_rs),
    .imm(jrcontrol_1_imm), .reg_write_e(jrcontrol_1_reg_write_e), .imm_sel(jrcontrol_1_imm_sel),
    .ALU_code(jrcontrol_1_alu_code), .is_j(jrcontrol_1_is_j), .is_jr_or_jalr(jrcontrol_1_is_jr_or_jalr));
  jalrControl jalrcontrol_1 (
    .data(sixbitdemultiplexer_1_jalroutput), .rd(jalrcontrol_1_rd), .rt(jalrcontrol_1_rt),
    .rs(jalrcontrol_1_rs), .imm(jalrcontrol_1_imm), .reg_write_e(jalrcontrol_1_reg_write_e),
    .imm_sel(jalrcontrol_1_imm_sel), .ALU_code(jalrcontrol_1_alu_code), .is_j(jalrcontrol_1_is_j),
    .is_jal_or_jalr(jalrcontrol_1_is_jal_or_jalr), .is_jr_or_jalr(jalrcontrol_1_is_jr_or_jalr));
  syscallControl syscallcontrol_1 (
    .data(sixbitdemultiplexer_1_syscalloutput), .rd(syscallcontrol_1_rd), .rt(syscallcontrol_1_rt),
    .rs(syscallcontrol_1_rs), .imm(syscallcontrol_1_imm), .reg_write_e(syscallcontrol_1_reg_write_e),
    .imm_sel(syscallcontrol_1_imm_sel), .ALU_code(syscallcontrol_1_alu_code), .is_j(syscallcontrol_1_is_j),
    .is_jal_or_jalr(syscallcontrol_1_is_jal_or_jalr), .is_jr_or_jalr(syscallcontrol_1_is_jr_or_jalr));
  lwControl lwcontrol_1 (
    .in_1(sixbitdemultiplexer_1_lwoutput), .rs(lwcontrol_1_rs), .rt(lwcontrol_1_rt), .rd(lwcontrol_1_rd),
    .imm(lwcontrol_1_imm), .reg_write_e(lwcontrol_1_reg_write_e), .imm_sel(lwcontrol_1_imm_sel),
    .ALU_code(lwcontrol_1_alu_code), .ALU_mem_sel(lwcontrol_1_alu_mem_sel));
  swControl swcontrol_1 (
    .in_1(sixbitdemultiplexer_1_swoutput), .rs(swcontrol_1_rs), .rt(swcontrol_1_rt), .rd(swcontrol_1_rd),
    .imm(swcontrol_1_imm), .reg_write_e(swcontrol_1_reg_write_e), .imm_sel(swcontrol_1_imm_sel),
    .ALU_code(swcontrol_1_alu_code), .WE_mem(swcontrol_1_we_mem));
  beqControl beqcontrol_1 (
    .in_1(sixbitdemultiplexer_1_beqoutput), .rs(beqcontrol_1_rs), .rt(beqcontrol_1_rt), .rd(beqcontrol_1_rd),
    .imm(beqcontrol_1_imm), .reg_write_e(beqcontrol_1_reg_write_e), .imm_sel(beqcontrol_1_imm_sel),
    .ALU_code(beqcontrol_1_alu_code), .is_beq(beqcontrol_1_is_beq));
  bneControl bnecontrol_1 (
    .in_1(sixbitdemultiplexer_1_bneoutput), .rs(bnecontrol_1_rs), .rt(bnecontrol_1_rt), .rd(bnecontrol_1_rd),
    .imm(bnecontrol_1_imm), .reg_write_e(bnecontrol_1_reg_write_e), .imm_sel(bnecontrol_1_imm_sel),
    .ALU_code(bnecontrol_1_alu_code), .is_bne(bnecontrol_1_is_bne));
  jControl jcontrol_1 (.data(sixbitdemultiplexer_1_joutput), .imm(jcontrol_1_imm), .is_j(jcontrol_1_is_j));
  jalControl jalcontrol_1 (
    .data(sixbitdemultiplexer_1_jaloutput), .imm(jalcontrol_1_imm), .rd(jalcontrol_1_rd),
    .is_j(jalcontrol_1_is_j), .is_jal_or_jalr(jalcontrol_1_is_jal_or_jalr),
    .reg_write_e(jalcontrol_1_reg_write_e));
  assign rd = mfhicontrol_1_rd | mflocontrol_1_rd | addcontrol_1_rd | subcontrol_1_rd | multcontrol_1_rd | divcontrol_1_rd | sllcontrol_1_rd | srlcontrol_1_rd | sltcontrol_1_rd | andcontrol_1_rd | orcontrol_1_rd | xorcontrol_1_rd | norcontrol_1_rd | addicontrol_1_rd | jrcontrol_1_rd | jalrcontrol_1_rd | syscallcontrol_1_rd | lwcontrol_1_rd | swcontrol_1_rd | beqcontrol_1_rd | bnecontrol_1_rd | jalcontrol_1_rd;  // OR_Gate or_1, 5 bits wide
  assign rt = sltcontrol_1_rt | andcontrol_1_rt | orcontrol_1_rt | xorcontrol_1_rt | norcontrol_1_rt | addicontrol_1_rt | addcontrol_1_rt | subcontrol_1_rt | multcontrol_1_rt | divcontrol_1_rt | mflocontrol_1_rt | mfhicontrol_1_rt | sllcontrol_1_rt | srlcontrol_1_rt | jrcontrol_1_rt | jalrcontrol_1_rt | syscallcontrol_1_rt | lwcontrol_1_rt | swcontrol_1_rt | beqcontrol_1_rt | bnecontrol_1_rt;  // OR_Gate or_2, 5 bits wide
  assign rs = addcontrol_1_rs | subcontrol_1_rs | multcontrol_1_rs | divcontrol_1_rs | mflocontrol_1_rs | mfhicontrol_1_rs | sllcontrol_1_rs | srlcontrol_1_rs | sltcontrol_1_rs | andcontrol_1_rs | orcontrol_1_rs | xorcontrol_1_rs | norcontrol_1_rs | addicontrol_1_rs | jrcontrol_1_rs | jalrcontrol_1_rs | syscallcontrol_1_rs | lwcontrol_1_rs | swcontrol_1_rs | beqcontrol_1_rs | bnecontrol_1_rs;  // OR_Gate or_3, 5 bits wide
  assign imm = addcontrol_1_imm | subcontrol_1_imm | multcontrol_1_imm | divcontrol_1_imm | mflocontrol_1_imm | mfhicontrol_1_imm | sllcontrol_1_imm | srlcontrol_1_imm | sltcontrol_1_imm | andcontrol_1_imm | orcontrol_1_imm | xorcontrol_1_imm | norcontrol_1_imm | addicontrol_1_imm | jrcontrol_1_imm | jalrcontrol_1_imm | syscallcontrol_1_imm | lwcontrol_1_imm | swcontrol_1_imm | beqcontrol_1_imm | bnecontrol_1_imm | jcontrol_1_imm | jalcontrol_1_imm;  // OR_Gate or_4, 32 bits wide
  or or_5 (reg_write_e, addcontrol_1_reg_write_e, subcontrol_1_reg_write_e, multcontrol_1_reg_write_e, divcontrol_1_reg_write_e, mflocontrol_1_reg_write_e, mfhicontrol_1_reg_write_e, sllcontrol_1_reg_write_e, srlcontrol_1_reg_write_e, sltcontrol_1_reg_write_e, andcontrol_1_reg_write_e, orcontrol_1_reg_write_e, xorcontrol_1_reg_write_e, norcontrol_1_reg_write_e, addicontrol_1_reg_write_e, jrcontrol_1_reg_write_e, jalrcontrol_1_reg_write_e, syscallcontrol_1_reg_write_e, lwcontrol_1_reg_write_e, swcontrol_1_reg_write_e, beqcontrol_1_reg_write_e, bnecontrol_1_reg_write_e, jalcontrol_1_reg_write_e);
  or or_6 (imm_sel, addcontrol_1_imm_sel, subcontrol_1_imm_sel, multcontrol_1_imm_sel, divcontrol_1_imm_sel, mflocontrol_1_imm_sel, mfhicontrol_1_imm_sel, sllcontrol_1_imm_sel, srlcontrol_1_imm_sel, sltcontrol_1_imm_sel, andcontrol_1_imm_sel, orcontrol_1_imm_sel, xorcontrol_1_imm_sel, norcontrol_1_imm_sel, addicontrol_1_imm_sel, jrcontrol_1_imm_sel, jalrcontrol_1_imm_sel, syscallcontrol_1_imm_sel, lwcontrol_1_imm_sel, swcontrol_1_imm_sel, beqcontrol_1_imm_sel, bnecontrol_1_imm_sel);
  assign ALU_code = addcontrol_1_alu_code | subcontrol_1_alu_code | multcontrol_1_alu_code | divcontrol_1_alu_code | mflocontrol_1_alu_code | mfhicontrol_1_alu_code | sllcontrol_1_alu_code | srlcontrol_1_alu_code | sltcontrol_1_alu_code | andcontrol_1_alu_code | orcontrol_1_alu_code | xorcontrol_1_alu_code | norcontrol_1_alu_code | addicontrol_1_alu_code | jrcontrol_1_alu_code | jalrcontrol_1_alu_code | syscallcontrol_1_alu_code | lwcontrol_1_alu_code | swcontrol_1_alu_code | bnecontrol_1_alu_code | beqcontrol_1_alu_code;  // OR_Gate or_7, 5 bits wide
  buf or_8 (is_beq, beqcontrol_1_is_beq);  // OR_Gate
  buf or_9 (is_bne, bnecontrol_1_is_bne);  // OR_Gate
  or or_10 (is_j, jrcontrol_1_is_j, jalrcontrol_1_is_j, syscallcontrol_1_is_j, jcontrol_1_is_j, jalcontrol_1_is_j);
  or or_11 (is_jal_or_jalr, jalrcontrol_1_is_jal_or_jalr, syscallcontrol_1_is_jal_or_jalr, jalcontrol_1_is_jal_or_jalr);
  or or_12 (is_jr_or_jalr, jrcontrol_1_is_jr_or_jalr, jalrcontrol_1_is_jr_or_jalr, syscallcontrol_1_is_jr_or_jalr);
  buf or_13 (WE_mem, swcontrol_1_we_mem);  // OR_Gate
  buf or_14 (ALU_mem_sel, lwcontrol_1_alu_mem_sel);  // OR_Gate

  // Notes on the sheet:
  //   rd
endmodule

module addControl (
  input  [31:0] data,
  output [4:0] rd,
  output [4:0] rt,
  output [4:0] rs,
  output [31:0] imm,
  output reg_write_e,
  output imm_sel,
  output [4:0] ALU_code
);

  wire comparator_1_gt;

  Comparator #(.mode("unsigned"), .width(32)) comparator_1 (
    .a(data), .b({32{1'b0}}), .gt(comparator_1_gt));  // open: eq, lt
  Multiplexer multiplexer_1 (.in0(1'b0), .in1(1'b1), .out(reg_write_e), .sel(comparator_1_gt));

  assign ALU_code = {5{1'b0}};
  assign imm = {32{1'b0}};
  assign imm_sel = 1'b0;
  assign rd = data[15:11];
  assign rs = data[25:21];
  assign rt = data[20:16];
endmodule

module subControl (
  input  [31:0] data,
  output [4:0] rd,
  output [4:0] rt,
  output [4:0] rs,
  output [31:0] imm,
  output reg_write_e,
  output imm_sel,
  output [4:0] ALU_code
);

  wire comparator_1_gt;

  Comparator #(.mode("unsigned"), .width(32)) comparator_1 (
    .a(data), .b({32{1'b0}}), .gt(comparator_1_gt));  // open: eq, lt
  Multiplexer #(.width(5)) multiplexer_1 (.in0({5{1'b0}}), .in1(5'b00001), .out(ALU_code), .sel(comparator_1_gt));
  Multiplexer multiplexer_2 (.in0(1'b0), .in1(1'b1), .out(reg_write_e), .sel(comparator_1_gt));

  assign imm = {32{1'b0}};
  assign imm_sel = 1'b0;
  assign rd = data[15:11];
  assign rs = data[25:21];
  assign rt = data[20:16];
endmodule

module mfloControl (
  input  [31:0] data,
  output [4:0] rd,
  output [4:0] rt,
  output [4:0] rs,
  output [31:0] imm,
  output reg_write_e,
  output imm_sel,
  output [4:0] ALU_code
);

  wire comparator_1_gt;

  Comparator #(.mode("unsigned"), .width(32)) comparator_1 (
    .a(data), .b({32{1'b0}}), .gt(comparator_1_gt));  // open: eq, lt
  Multiplexer multiplexer_1 (.in0(1'b0), .in1(1'b1), .out(reg_write_e), .sel(comparator_1_gt));
  Multiplexer #(.width(5)) multiplexer_2 (.in0({5{1'b0}}), .in1(5'b00100), .out(ALU_code), .sel(comparator_1_gt));

  assign imm = {32{1'b0}};
  assign imm_sel = 1'b0;
  assign rd = data[15:11];
  assign rs = {5{1'b0}};
  assign rt = {5{1'b0}};
endmodule

module multControl (
  input  [31:0] data,
  output [4:0] rd,
  output [4:0] rt,
  output [4:0] rs,
  output [31:0] imm,
  output reg_write_e,
  output imm_sel,
  output [4:0] ALU_code
);

  wire comparator_1_gt;

  Comparator #(.mode("unsigned"), .width(32)) comparator_1 (
    .a(data), .b({32{1'b0}}), .gt(comparator_1_gt));  // open: eq, lt
  Multiplexer #(.width(5)) multiplexer_1 (.in0({5{1'b0}}), .in1(5'b00010), .out(ALU_code), .sel(comparator_1_gt));

  assign imm = {32{1'b0}};
  assign imm_sel = 1'b0;
  assign rd = {5{1'b0}};
  assign reg_write_e = 1'b0;
  assign rs = data[25:21];
  assign rt = data[20:16];
endmodule

module srlControl (
  input  [31:0] data,
  output [31:0] imm,
  output [4:0] rd,
  output [4:0] rt,
  output [4:0] rs,
  output reg_write_e,
  output imm_sel,
  output [4:0] ALU_code
);

  wire comparator_1_gt;

  Comparator #(.mode("unsigned"), .width(32)) comparator_1 (
    .a(data), .b({32{1'b0}}), .gt(comparator_1_gt));  // open: eq, lt
  assign imm = {{27{data[10]}}, data[10:6]};  // Bit_Extender bit_extender_1
  Multiplexer #(.width(5)) multiplexer_1 (.in0({5{1'b0}}), .in1(5'b00111), .out(ALU_code), .sel(comparator_1_gt));
  Multiplexer multiplexer_2 (.in0(1'b0), .in1(1'b1), .out(reg_write_e), .sel(comparator_1_gt));
  Multiplexer multiplexer_3 (.in0(1'b0), .in1(1'b1), .out(imm_sel), .sel(comparator_1_gt));

  assign rd = data[15:11];
  assign rs = data[25:21];
  assign rt = data[20:16];
endmodule

module divControl (
  input  [31:0] data,
  output [4:0] rd,
  output [4:0] rt,
  output [4:0] rs,
  output [31:0] imm,
  output reg_write_e,
  output imm_sel,
  output [4:0] ALU_code
);

  wire comparator_1_gt;

  Comparator #(.mode("unsigned"), .width(32)) comparator_1 (
    .a(data), .b({32{1'b0}}), .gt(comparator_1_gt));  // open: eq, lt
  Multiplexer #(.width(5)) multiplexer_1 (.in0({5{1'b0}}), .in1(5'b00011), .out(ALU_code), .sel(comparator_1_gt));

  assign imm = {32{1'b0}};
  assign imm_sel = 1'b0;
  assign rd = {5{1'b0}};
  assign reg_write_e = 1'b0;
  assign rs = data[25:21];
  assign rt = data[20:16];
endmodule

module sllControl (
  input  [31:0] data,
  output [31:0] imm,
  output [4:0] rd,
  output [4:0] rt,
  output [4:0] rs,
  output reg_write_e,
  output imm_sel,
  output [4:0] ALU_code
);

  wire comparator_1_gt;

  Comparator #(.mode("unsigned"), .width(32)) comparator_1 (
    .a(data), .b({32{1'b0}}), .gt(comparator_1_gt));  // open: eq, lt
  assign imm = {{27{data[10]}}, data[10:6]};  // Bit_Extender bit_extender_1
  Multiplexer #(.width(5)) multiplexer_1 (.in0({5{1'b0}}), .in1(5'b00110), .out(ALU_code), .sel(comparator_1_gt));
  Multiplexer multiplexer_2 (.in0(1'b0), .in1(1'b1), .out(reg_write_e), .sel(comparator_1_gt));
  Multiplexer multiplexer_3 (.in0(1'b0), .in1(1'b1), .out(imm_sel), .sel(comparator_1_gt));

  assign rd = data[15:11];
  assign rs = data[25:21];
  assign rt = data[20:16];
endmodule

module orControl (
  input  [31:0] data,
  output [4:0] rd,
  output [4:0] rt,
  output [4:0] rs,
  output [31:0] imm,
  output reg_write_e,
  output imm_sel,
  output [4:0] ALU_code
);

  wire comparator_1_gt;

  Comparator #(.mode("unsigned"), .width(32)) comparator_1 (
    .a(data), .b({32{1'b0}}), .gt(comparator_1_gt));  // open: eq, lt
  Multiplexer multiplexer_1 (.in0(1'b0), .in1(1'b1), .out(reg_write_e), .sel(comparator_1_gt));
  Multiplexer #(.width(5)) multiplexer_2 (.in0({5{1'b0}}), .in1(5'b01000), .out(ALU_code), .sel(comparator_1_gt));

  assign imm = {32{1'b0}};
  assign imm_sel = 1'b0;
  assign rd = data[15:11];
  assign rs = data[25:21];
  assign rt = data[20:16];
endmodule

module mfhiControl (
  input  [31:0] in_1,
  output [4:0] rs,
  output [4:0] rt,
  output [4:0] rd,
  output [31:0] imm,
  output reg_write_e,
  output imm_sel,
  output [4:0] ALU_code
);

  wire comparator_1_gt;

  Comparator #(.mode("unsigned"), .width(32)) comparator_1 (
    .a(in_1), .b({32{1'b0}}), .gt(comparator_1_gt));  // open: eq, lt
  Multiplexer multiplexer_1 (.in0(1'b0), .in1(1'b1), .out(reg_write_e), .sel(comparator_1_gt));
  Multiplexer #(.width(5)) multiplexer_2 (.in0({5{1'b0}}), .in1(5'b00101), .out(ALU_code), .sel(comparator_1_gt));

  assign imm = {32{1'b0}};
  assign imm_sel = 1'b0;
  assign rd = in_1[15:11];
  assign rs = {5{1'b0}};
  assign rt = {5{1'b0}};
endmodule

module addiControl (
  input  [31:0] in_1,
  output [4:0] rs,
  output [4:0] rt,
  output [4:0] rd,
  output [31:0] imm,
  output reg_write_e,
  output imm_sel,
  output [4:0] ALU_code
);

  wire comparator_1_gt;

  Comparator #(.mode("unsigned"), .width(32)) comparator_1 (
    .a(in_1), .b({32{1'b0}}), .gt(comparator_1_gt));  // open: eq, lt
  assign imm = {{16{in_1[15]}}, in_1[15:0]};  // Bit_Extender bit_extender_1
  Multiplexer multiplexer_1 (.in0(1'b0), .in1(1'b1), .out(reg_write_e), .sel(comparator_1_gt));
  Multiplexer multiplexer_2 (.in0(1'b0), .in1(1'b1), .out(imm_sel), .sel(comparator_1_gt));
  Multiplexer #(.width(5)) multiplexer_3 (.in0({5{1'b0}}), .in1({5{1'b0}}), .out(ALU_code), .sel(comparator_1_gt));

  assign rd = in_1[20:16];
  assign rs = in_1[25:21];
  assign rt = {5{1'b0}};
endmodule

module andControl (
  input  [31:0] data,
  output [4:0] rd,
  output [4:0] rt,
  output [4:0] rs,
  output [31:0] imm,
  output reg_write_e,
  output imm_sel,
  output [4:0] ALU_code
);

  wire comparator_1_gt;

  Comparator #(.mode("unsigned"), .width(32)) comparator_1 (
    .a(data), .b({32{1'b0}}), .gt(comparator_1_gt));  // open: eq, lt
  Multiplexer multiplexer_1 (.in0(1'b0), .in1(1'b1), .out(reg_write_e), .sel(comparator_1_gt));
  Multiplexer #(.width(5)) multiplexer_2 (.in0({5{1'b0}}), .in1(5'b01011), .out(ALU_code), .sel(comparator_1_gt));

  assign imm = {32{1'b0}};
  assign imm_sel = 1'b0;
  assign rd = data[15:11];
  assign rs = data[25:21];
  assign rt = data[20:16];
endmodule

module norControl (
  input  [31:0] data,
  output [4:0] rd,
  output [4:0] rt,
  output [4:0] rs,
  output [31:0] imm,
  output reg_write_e,
  output imm_sel,
  output [4:0] ALU_code
);

  wire comparator_1_gt;

  Comparator #(.mode("unsigned"), .width(32)) comparator_1 (
    .a(data), .b({32{1'b0}}), .gt(comparator_1_gt));  // open: eq, lt
  Multiplexer multiplexer_1 (.in0(1'b0), .in1(1'b1), .out(reg_write_e), .sel(comparator_1_gt));
  Multiplexer #(.width(5)) multiplexer_2 (.in0({5{1'b0}}), .in1(5'b01001), .out(ALU_code), .sel(comparator_1_gt));

  assign imm = {32{1'b0}};
  assign imm_sel = 1'b0;
  assign rd = data[15:11];
  assign rs = data[25:21];
  assign rt = data[20:16];
endmodule

module lwControl (
  input  [31:0] in_1,
  output [4:0] rs,
  output [4:0] rt,
  output [4:0] rd,
  output [31:0] imm,
  output reg_write_e,
  output imm_sel,
  output [4:0] ALU_code,
  output ALU_mem_sel
);

  wire comparator_1_gt;

  Comparator #(.mode("unsigned"), .width(32)) comparator_1 (
    .a(in_1), .b({32{1'b0}}), .gt(comparator_1_gt));  // open: eq, lt
  assign imm = {{16{in_1[15]}}, in_1[15:0]};  // Bit_Extender bit_extender_1
  Multiplexer multiplexer_1 (.in0(1'b0), .in1(1'b1), .out(reg_write_e), .sel(comparator_1_gt));
  Multiplexer multiplexer_2 (.in0(1'b0), .in1(1'b1), .out(imm_sel), .sel(comparator_1_gt));
  Multiplexer #(.width(5)) multiplexer_3 (.in0({5{1'b0}}), .in1({5{1'b0}}), .out(ALU_code), .sel(comparator_1_gt));
  Multiplexer multiplexer_4 (.in0(1'b0), .in1(1'b1), .out(ALU_mem_sel), .sel(comparator_1_gt));

  assign rd = in_1[20:16];
  assign rs = in_1[25:21];
  assign rt = {5{1'b0}};
endmodule

module xorControl (
  input  [31:0] data,
  output [4:0] rd,
  output [4:0] rt,
  output [4:0] rs,
  output [31:0] imm,
  output reg_write_e,
  output imm_sel,
  output [4:0] ALU_code
);

  wire comparator_1_gt;

  Comparator #(.mode("unsigned"), .width(32)) comparator_1 (
    .a(data), .b({32{1'b0}}), .gt(comparator_1_gt));  // open: eq, lt
  Multiplexer multiplexer_1 (.in0(1'b0), .in1(1'b1), .out(reg_write_e), .sel(comparator_1_gt));
  Multiplexer #(.width(5)) multiplexer_2 (.in0({5{1'b0}}), .in1(5'b01010), .out(ALU_code), .sel(comparator_1_gt));

  assign imm = {32{1'b0}};
  assign imm_sel = 1'b0;
  assign rd = data[15:11];
  assign rs = data[25:21];
  assign rt = data[20:16];
endmodule

module swControl (
  input  [31:0] in_1,
  output [4:0] rs,
  output [4:0] rt,
  output [4:0] rd,
  output [31:0] imm,
  output reg_write_e,
  output imm_sel,
  output [4:0] ALU_code,
  output WE_mem
);

  wire comparator_1_gt;

  Comparator #(.mode("unsigned"), .width(32)) comparator_1 (
    .a(in_1), .b({32{1'b0}}), .gt(comparator_1_gt));  // open: eq, lt
  assign imm = {{16{in_1[15]}}, in_1[15:0]};  // Bit_Extender bit_extender_1
  Multiplexer multiplexer_1 (.in0(1'b0), .in1(1'b0), .out(reg_write_e), .sel(comparator_1_gt));
  Multiplexer multiplexer_2 (.in0(1'b0), .in1(1'b1), .out(imm_sel), .sel(comparator_1_gt));
  Multiplexer #(.width(5)) multiplexer_3 (.in0({5{1'b0}}), .in1({5{1'b0}}), .out(ALU_code), .sel(comparator_1_gt));
  Multiplexer multiplexer_4 (.in0(1'b0), .in1(1'b1), .out(WE_mem), .sel(comparator_1_gt));

  assign rd = {5{1'b0}};
  assign rs = in_1[25:21];
  assign rt = in_1[20:16];
endmodule

module beqControl (
  input  [31:0] in_1,
  output [4:0] rs,
  output [4:0] rt,
  output [4:0] rd,
  output [31:0] imm,
  output reg_write_e,
  output imm_sel,
  output [4:0] ALU_code,
  output is_beq
);

  wire comparator_1_gt;

  Comparator #(.mode("unsigned"), .width(32)) comparator_1 (
    .a(in_1), .b({32{1'b0}}), .gt(comparator_1_gt));  // open: eq, lt
  assign imm = {{16{in_1[15]}}, in_1[15:0]};  // Bit_Extender bit_extender_1
  Multiplexer multiplexer_1 (.in0(1'b0), .in1(1'b0), .out(reg_write_e), .sel(comparator_1_gt));
  Multiplexer multiplexer_2 (.in0(1'b0), .in1(1'b0), .out(imm_sel), .sel(comparator_1_gt));
  Multiplexer #(.width(5)) multiplexer_3 (.in0({5{1'b0}}), .in1({5{1'b0}}), .out(ALU_code), .sel(comparator_1_gt));
  Multiplexer multiplexer_4 (.in0(1'b0), .in1(1'b1), .out(is_beq), .sel(comparator_1_gt));

  assign rd = {5{1'b0}};
  assign rs = in_1[25:21];
  assign rt = in_1[20:16];
endmodule

module bneControl (
  input  [31:0] in_1,
  output [4:0] rs,
  output [4:0] rt,
  output [4:0] rd,
  output [31:0] imm,
  output reg_write_e,
  output imm_sel,
  output [4:0] ALU_code,
  output is_bne
);

  wire comparator_1_gt;

  Comparator #(.mode("unsigned"), .width(32)) comparator_1 (
    .a(in_1), .b({32{1'b0}}), .gt(comparator_1_gt));  // open: eq, lt
  assign imm = {{16{in_1[15]}}, in_1[15:0]};  // Bit_Extender bit_extender_1
  Multiplexer multiplexer_1 (.in0(1'b0), .in1(1'b0), .out(reg_write_e), .sel(comparator_1_gt));
  Multiplexer multiplexer_2 (.in0(1'b0), .in1(1'b0), .out(imm_sel), .sel(comparator_1_gt));
  Multiplexer #(.width(5)) multiplexer_3 (.in0({5{1'b0}}), .in1({5{1'b0}}), .out(ALU_code), .sel(comparator_1_gt));
  Multiplexer multiplexer_4 (.in0(1'b0), .in1(1'b1), .out(is_bne), .sel(comparator_1_gt));

  assign rd = {5{1'b0}};
  assign rs = in_1[25:21];
  assign rt = in_1[20:16];
endmodule

module sltControl (
  input  [31:0] data,
  output [4:0] rd,
  output [4:0] rt,
  output [4:0] rs,
  output [31:0] imm,
  output reg_write_e,
  output imm_sel,
  output [4:0] ALU_code
);

  wire comparator_1_gt;

  Comparator #(.mode("unsigned"), .width(32)) comparator_1 (
    .a(data), .b({32{1'b0}}), .gt(comparator_1_gt));  // open: eq, lt
  Multiplexer multiplexer_1 (.in0(1'b0), .in1(1'b1), .out(reg_write_e), .sel(comparator_1_gt));
  Multiplexer #(.width(5)) multiplexer_2 (.in0({5{1'b0}}), .in1(5'b01100), .out(ALU_code), .sel(comparator_1_gt));

  assign imm = {32{1'b0}};
  assign imm_sel = 1'b0;
  assign rd = data[15:11];
  assign rs = data[25:21];
  assign rt = data[20:16];
endmodule

module jControl (
  input  [31:0] data,
  output [31:0] imm,
  output is_j
);

  wire comparator_1_gt;
  wire [25:0] multiplexer_1_out;

  Comparator #(.mode("unsigned"), .width(32)) comparator_1 (
    .a(data), .b({32{1'b0}}), .gt(comparator_1_gt));  // open: eq, lt
  Multiplexer #(.width(26)) multiplexer_1 (
    .in0({26{1'b0}}), .in1(data[31:6]), .out(multiplexer_1_out), .sel(comparator_1_gt));
  Multiplexer multiplexer_2 (.in0(1'b0), .in1(1'b1), .out(is_j), .sel(comparator_1_gt));
  assign imm = {{6{multiplexer_1_out[25]}}, multiplexer_1_out};  // Bit_Extender bit_extender_1
endmodule

module jalControl (
  input  [31:0] data,
  output [31:0] imm,
  output [4:0] rd,
  output is_j,
  output is_jal_or_jalr,
  output reg_write_e
);

  wire comparator_1_gt;
  wire [25:0] multiplexer_1_out;

  Comparator #(.mode("unsigned"), .width(32)) comparator_1 (
    .a(data), .b({32{1'b0}}), .gt(comparator_1_gt));  // open: eq, lt
  Multiplexer #(.width(26)) multiplexer_1 (
    .in0({26{1'b0}}), .in1(data[31:6]), .out(multiplexer_1_out), .sel(comparator_1_gt));
  Multiplexer multiplexer_2 (.in0(1'b0), .in1(1'b1), .out(is_j), .sel(comparator_1_gt));
  assign imm = {{6{multiplexer_1_out[25]}}, multiplexer_1_out};  // Bit_Extender bit_extender_1
  Multiplexer multiplexer_3 (.in0(1'b0), .in1(1'b1), .out(is_jal_or_jalr), .sel(comparator_1_gt));
  Multiplexer #(.width(5)) multiplexer_4 (.in0({5{1'b0}}), .in1({5{1'b1}}), .out(rd), .sel(comparator_1_gt));
  Multiplexer multiplexer_5 (.in0(1'b0), .in1(1'b1), .out(reg_write_e), .sel(comparator_1_gt));
endmodule

module jalrControl (
  input  [31:0] data,
  output [4:0] rd,
  output [4:0] rt,
  output [4:0] rs,
  output [31:0] imm,
  output reg_write_e,
  output imm_sel,
  output [4:0] ALU_code,
  output is_j,
  output is_jal_or_jalr,
  output is_jr_or_jalr
);

  wire comparator_1_gt;

  Comparator #(.mode("unsigned"), .width(32)) comparator_1 (
    .a(data), .b({32{1'b0}}), .gt(comparator_1_gt));  // open: eq, lt
  Multiplexer multiplexer_1 (.in0(1'b0), .in1(1'b1), .out(reg_write_e), .sel(comparator_1_gt));
  Multiplexer #(.width(5)) multiplexer_2 (.in0({5{1'b0}}), .in1({5{1'b0}}), .out(ALU_code), .sel(comparator_1_gt));
  Multiplexer multiplexer_3 (.in0(1'b0), .in1(1'b1), .out(is_j), .sel(comparator_1_gt));
  Multiplexer multiplexer_4 (.in0(1'b0), .in1(1'b1), .out(is_jal_or_jalr), .sel(comparator_1_gt));
  Multiplexer multiplexer_5 (.in0(1'b0), .in1(1'b1), .out(is_jr_or_jalr), .sel(comparator_1_gt));

  assign imm = {32{1'b0}};
  assign imm_sel = 1'b0;
  assign rd = data[15:11];
  assign rs = data[25:21];
  assign rt = {5{1'b0}};
endmodule

module jrControl (
  input  [31:0] data,
  output [4:0] rd,
  output [4:0] rt,
  output [4:0] rs,
  output [31:0] imm,
  output reg_write_e,
  output imm_sel,
  output [4:0] ALU_code,
  output is_j,
  output is_jr_or_jalr
);

  wire comparator_1_gt;

  Comparator #(.mode("unsigned"), .width(32)) comparator_1 (
    .a(data), .b({32{1'b0}}), .gt(comparator_1_gt));  // open: eq, lt
  Multiplexer multiplexer_1 (.in0(1'b0), .in1(1'b0), .out(reg_write_e), .sel(comparator_1_gt));
  Multiplexer #(.width(5)) multiplexer_2 (.in0({5{1'b0}}), .in1({5{1'b0}}), .out(ALU_code), .sel(comparator_1_gt));
  Multiplexer multiplexer_3 (.in0(1'b0), .in1(1'b1), .out(is_j), .sel(comparator_1_gt));
  Multiplexer #(.width(5)) multiplexer_4 (.in0({5{1'b0}}), .in1({5{1'b0}}), .out(rd), .sel(comparator_1_gt));
  Multiplexer multiplexer_5 (.in0(1'b0), .in1(1'b1), .out(is_jr_or_jalr), .sel(comparator_1_gt));

  assign imm = {32{1'b0}};
  assign imm_sel = 1'b0;
  assign rs = data[25:21];
  assign rt = {5{1'b0}};
endmodule

module syscallControl (
  input  [31:0] data,
  output [4:0] rd,
  output [4:0] rt,
  output [4:0] rs,
  output [31:0] imm,
  output reg_write_e,
  output imm_sel,
  output [4:0] ALU_code,
  output is_j,
  output is_jal_or_jalr,
  output is_jr_or_jalr
);

  wire comparator_1_gt;

  Comparator #(.mode("unsigned"), .width(32)) comparator_1 (
    .a(data), .b({32{1'b0}}), .gt(comparator_1_gt));  // open: eq, lt
  Multiplexer multiplexer_1 (.in0(1'b0), .in1(1'b1), .out(reg_write_e), .sel(comparator_1_gt));
  Multiplexer #(.width(5)) multiplexer_2 (.in0({5{1'b0}}), .in1({5{1'b0}}), .out(ALU_code), .sel(comparator_1_gt));
  Multiplexer multiplexer_3 (.in0(1'b0), .in1(1'b1), .out(is_j), .sel(comparator_1_gt));
  Multiplexer #(.width(5)) multiplexer_4 (.in0({5{1'b0}}), .in1(5'b11010), .out(rd), .sel(comparator_1_gt));
  Multiplexer multiplexer_5 (.in0(1'b0), .in1(1'b1), .out(is_jal_or_jalr), .sel(comparator_1_gt));
  Multiplexer multiplexer_6 (.in0(1'b0), .in1(1'b1), .out(is_jr_or_jalr), .sel(comparator_1_gt));

  assign imm = {32{1'b0}};
  assign imm_sel = 1'b0;
  assign rs = {5{1'b0}};
  assign rt = {5{1'b0}};
endmodule

module Computer (
);

  wire clock_1_out, clock_2_out, clock_3_out, cpumain_1_buswe, joystickcontroller_1_writeenabletobus,
       keyboard_1_avail, keyboardcontroller_1_keyboardread, keyboardcontroller_1_writetobus,
       ledcontroller_1_ledstate, memorycontrollertest_1_writeenabletomem, memorycontrollertest_1_writetobus,
       rgb_video_1_p1, rgb_video_1_p2, soundcontrollersine_1_enablesound,
       soundcontrollersquare_1_enablesound, soundcontrollertriangle_1_enablesound,
       terminalcontroller_1_writetoterminal;
  wire [3:0] joystick_1_x, joystick_1_y;
  wire [6:0] keyboard_1_data, soundcontrollersine_1_volume, soundcontrollersquare_1_volume,
       soundcontrollertriangle_1_volume, terminalcontroller_1_datatoterminal;
  wire [7:0] rgb_video_1_p3, rgb_video_1_p4;
  wire [13:0] soundcontrollersine_1_frequency, soundcontrollersquare_1_frequency,
       soundcontrollertriangle_1_frequency;
  wire [23:0] memorycontrollertest_1_addresstomem, rgb_video_1_p5;
  wire [25:0] cpumain_1_addresstobus;
  wire [31:0] controlled_buffer_1_out, cpumain_1_datatobus, joystickcontroller_1_datatobus,
       keyboardcontroller_1_datatobus, memorycontrollertest_1_datatobus, memorycontrollertest_1_datatomem,
       ram_1_dout;

  RAM #(.addrWidth(24), .dataWidth(32), .enables("line")) ram_1 (
    .addr(memorycontrollertest_1_addresstomem), .we(memorycontrollertest_1_writeenabletomem),
    .clk(clock_1_out), .din(memorycontrollertest_1_datatomem), .dout(ram_1_dout));
  Clock clock_1 (.out(clock_1_out));
  Clock clock_2 (.out(clock_2_out));
  Keyboard keyboard_1 (
    .clk(clock_2_out), .re(keyboardcontroller_1_keyboardread), .avail(keyboard_1_avail),
    .data(keyboard_1_data));  // open: clr
  MemoryControllerTest memorycontrollertest_1 (
    .WriteEnableFromBus(cpumain_1_buswe), .AddressFromBus(cpumain_1_addresstobus),
    .DataFromBus(controlled_buffer_1_out), .DataFromMem(ram_1_dout),
    .WriteToBus(memorycontrollertest_1_writetobus), .DataToBus(memorycontrollertest_1_datatobus),
    .AddressToMem(memorycontrollertest_1_addresstomem),
    .WriteEnableToMem(memorycontrollertest_1_writeenabletomem), .DataToMem(memorycontrollertest_1_datatomem));
  CPUmain cpumain_1 (
    .DataFromBus(controlled_buffer_1_out), .AddressToBus(cpumain_1_addresstobus), .BusWE(cpumain_1_buswe),
    .DataToBus(cpumain_1_datatobus));
  assign controlled_buffer_1_out = memorycontrollertest_1_writetobus ? memorycontrollertest_1_datatobus : 32'bz;  // Controlled_Buffer controlled_buffer_1
  assign controlled_buffer_1_out = cpumain_1_buswe ? cpumain_1_datatobus : 32'bz;  // Controlled_Buffer controlled_buffer_2
  KeyboardController keyboardcontroller_1 (
    .WriteEnableFromBus(cpumain_1_buswe), .AddressFromBus(cpumain_1_addresstobus),
    .KeyboardData(keyboard_1_data), .DataFromBus(controlled_buffer_1_out), .KeyboardStatus(keyboard_1_avail),
    .DataToBus(keyboardcontroller_1_datatobus), .WriteToBus(keyboardcontroller_1_writetobus),
    .KeyboardRead(keyboardcontroller_1_keyboardread));
  assign controlled_buffer_1_out = keyboardcontroller_1_writetobus ? keyboardcontroller_1_datatobus : 32'bz;  // Controlled_Buffer controlled_buffer_3
  TTY tty_1 (
    .data(terminalcontroller_1_datatoterminal), .clk(clock_3_out), .we(terminalcontroller_1_writetoterminal));  // open: clr
  Clock clock_3 (.out(clock_3_out));
  // RGB_Video #(.height(256), .scale(1), .width(256)) rgb_video_1: pin names not known; wires that end beside it: rgb_video_1_p1, rgb_video_1_p2, rgb_video_1_p3, rgb_video_1_p4, rgb_video_1_p5
  Clock clock_4 (.out(rgb_video_1_p1));
  TerminalController terminalcontroller_1 (
    .WriteEnableFromBus(cpumain_1_buswe), .AddressFromBus(cpumain_1_addresstobus),
    .DataFromBus(controlled_buffer_1_out), .WriteToTerminal(terminalcontroller_1_writetoterminal),
    .DataToTerminal(terminalcontroller_1_datatoterminal));
  RGBController rgbcontroller_1 (
    .AddressFromBus(cpumain_1_addresstobus), .WriteEnable(cpumain_1_buswe),
    .DataFromBus(controlled_buffer_1_out), .RGBX(rgb_video_1_p3), .RGBY(rgb_video_1_p4),
    .RGBColor(rgb_video_1_p5), .RGBWrite(rgb_video_1_p2));
  LEDController ledcontroller_1 (
    .AddressFromBus(cpumain_1_addresstobus), .WriteEnable(cpumain_1_buswe),
    .DataFromBus(controlled_buffer_1_out), .LEDState(ledcontroller_1_ledstate));
  Joystick joystick_1 (.x(joystick_1_x), .y(joystick_1_y));
  SoundControllerSine soundcontrollersine_1 (
    .DataFromBus(controlled_buffer_1_out), .AddressFromBus(cpumain_1_addresstobus),
    .WriteEnableFromBus(cpumain_1_buswe), .Frequency(soundcontrollersine_1_frequency),
    .EnableSound(soundcontrollersine_1_enablesound), .Volume(soundcontrollersine_1_volume));
  SoundControllerTriangle soundcontrollertriangle_1 (
    .Frequency(soundcontrollertriangle_1_frequency), .EnableSound(soundcontrollertriangle_1_enablesound),
    .Volume(soundcontrollertriangle_1_volume));  // open: DataFromBus, AddressFromBus, WriteEnableFromBus
  SoundControllerSquare soundcontrollersquare_1 (
    .Frequency(soundcontrollersquare_1_frequency), .EnableSound(soundcontrollersquare_1_enablesound),
    .Volume(soundcontrollersquare_1_volume));  // open: DataFromBus, AddressFromBus, WriteEnableFromBus
  LED led_1 (.in(ledcontroller_1_ledstate));
  assign controlled_buffer_1_out = joystickcontroller_1_writeenabletobus ? joystickcontroller_1_datatobus : 32'bz;  // Controlled_Buffer controlled_buffer_4
  JoystickController joystickcontroller_1 (
    .DataFromBus(controlled_buffer_1_out), .WriteEnableFromBus(cpumain_1_buswe),
    .AddressFromBus(cpumain_1_addresstobus), .X(joystick_1_x), .Y(joystick_1_y),
    .WriteEnableToBus(joystickcontroller_1_writeenabletobus), .DataToBus(joystickcontroller_1_datatobus));
  // Probe on soundcontrollersine_1_frequency
  // Probe on soundcontrollersquare_1_frequency
  // Buzzer #(.smooth_level(10), .smooth_width(10)) buzzer_1: pin names not known; wires that end beside it: soundcontrollersine_1_frequency, soundcontrollersine_1_enablesound, 7'b0111001
  // Probe on soundcontrollersine_1_volume
  // Buzzer #(.waveform("Triangle")) buzzer_2: pin names not known; wires that end beside it: soundcontrollertriangle_1_frequency, soundcontrollertriangle_1_enablesound, soundcontrollertriangle_1_volume
  // Buzzer buzzer_3: pin names not known; wires that end beside it: soundcontrollersquare_1_frequency, soundcontrollersquare_1_enablesound, soundcontrollersquare_1_volume
  // Probe on soundcontrollersquare_1_volume

  // Notes on the sheet:
  //   Write_enable
  //   Address
  //   Data
endmodule

module CPU (
  input  [31:0] DataFromBus,
  output [31:0] DataToBus,
  output [25:0] AddressToBus,
  output BusWriteEnable
);


  assign BusWriteEnable = 1'b0;

  // Notes on the sheet:
  //   delete this constant 0
endmodule

module MemoryControllerTest (
  input  WriteEnableFromBus,
  input  [25:0] AddressFromBus,
  input  [31:0] DataFromBus,
  input  [31:0] DataFromMem,
  output WriteToBus,
  output [31:0] DataToBus,
  output WriteEnableToMem,
  output [23:0] AddressToMem,
  output [31:0] DataToMem
);

  wire comparator_1_lt;
  wire [25:0] shifter_1_out;

  Comparator #(.mode("unsigned"), .width(26)) comparator_1 (
    .a(AddressFromBus), .b(26'h3ffff00), .lt(comparator_1_lt));  // open: gt, eq
  and and_1 (WriteEnableToMem, comparator_1_lt, WriteEnableFromBus);
  and and_2 (WriteToBus, comparator_1_lt, ~WriteEnableFromBus);  // AND_Gate
  Shifter #(.shift("lr"), .width(26)) shifter_1 (.in(AddressFromBus), .\dist (5'b00010), .out(shifter_1_out));
  Bit_Extender #(.in_width(26), .out_width(24)) bit_extender_1 (.in(shifter_1_out), .out(AddressToMem));

  assign DataToBus = DataFromMem;
  assign DataToMem = DataFromBus;
endmodule

module KeyboardController (
  input  [31:0] DataFromBus,
  input  WriteEnableFromBus,
  input  [25:0] AddressFromBus,
  input  [6:0] KeyboardData,
  input  KeyboardStatus,
  output KeyboardRead,
  output WriteToBus,
  output [31:0] DataToBus
);

  wire and_2_out, and_3_out, comparator_1_eq, comparator_2_eq, multiplexer_1_out, not_1_out;
  wire [6:0] multiplexer_2_out;
  wire [31:0] bit_extender_1_out, bit_extender_2_out;

  not not_1 (not_1_out, WriteEnableFromBus);
  Comparator #(.width(26)) comparator_1 (.a(26'h3ffff10), .b(AddressFromBus), .eq(comparator_1_eq));  // open: gt, lt
  Comparator #(.width(26)) comparator_2 (.a(26'h3ffff14), .b(AddressFromBus), .eq(comparator_2_eq));  // open: gt, lt
  and and_1 (KeyboardRead, comparator_1_eq, WriteEnableFromBus);
  and and_2 (and_2_out, not_1_out, comparator_1_eq);
  Multiplexer multiplexer_1 (.in0(1'b0), .in1(KeyboardStatus), .out(multiplexer_1_out), .sel(and_2_out));
  and and_3 (and_3_out, not_1_out, comparator_2_eq);
  assign bit_extender_1_out = {{31{multiplexer_1_out}}, multiplexer_1_out};  // Bit_Extender bit_extender_1
  Multiplexer #(.width(7)) multiplexer_2 (
    .in0({7{1'b0}}), .in1(KeyboardData), .out(multiplexer_2_out), .sel(and_3_out));
  or or_1 (WriteToBus, comparator_1_eq, comparator_2_eq);
  assign bit_extender_2_out = {{25{1'b0}}, multiplexer_2_out};  // Bit_Extender bit_extender_2
  assign DataToBus = bit_extender_1_out | bit_extender_2_out;  // OR_Gate or_2, 32 bits wide

  // Notes on the sheet:
  //   keyboard status address
  //   keyboard data address
endmodule

module RGBController (
  input  [25:0] AddressFromBus,
  input  WriteEnable,
  input  [31:0] DataFromBus,
  output [7:0] RGBX,
  output [7:0] RGBY,
  output [23:0] RGBColor,
  output RGBWrite
);

  wire and_1_out, and_2_out, and_3_out, clock_1_out, clock_2_out, clock_3_out, comparator_1_eq,
       comparator_2_eq, comparator_3_eq, comparator_4_eq;
  wire [7:0] bit_extender_1_out, bit_extender_2_out;
  wire [23:0] bit_extender_3_out;
  wire [31:0] multiplexer_1_out, multiplexer_2_out, multiplexer_3_out;

  Comparator #(.width(26)) comparator_1 (.a(26'h3ffff20), .b(AddressFromBus), .eq(comparator_1_eq));  // open: gt, lt
  Comparator #(.width(26)) comparator_2 (.a(26'h3ffff24), .b(AddressFromBus), .eq(comparator_2_eq));  // open: gt, lt
  Comparator #(.width(26)) comparator_3 (.a(26'h3ffff28), .b(AddressFromBus), .eq(comparator_3_eq));  // open: gt, lt
  Comparator #(.width(26)) comparator_4 (.a(26'h3ffff2c), .b(AddressFromBus), .eq(comparator_4_eq));  // open: gt, lt
  and and_1 (and_1_out, WriteEnable, comparator_1_eq);
  and and_2 (and_2_out, WriteEnable, comparator_2_eq);
  and and_3 (and_3_out, WriteEnable, comparator_3_eq);
  and and_4 (RGBWrite, WriteEnable, comparator_4_eq);
  Multiplexer #(.width(32)) multiplexer_1 (.in1(DataFromBus), .out(multiplexer_1_out), .sel(and_1_out));  // open: in0
  Multiplexer #(.width(32)) multiplexer_2 (.in1(DataFromBus), .out(multiplexer_2_out), .sel(and_2_out));  // open: in0
  Multiplexer #(.width(32)) multiplexer_3 (.in1(DataFromBus), .out(multiplexer_3_out), .sel(and_3_out));  // open: in0
  Bit_Extender #(.in_width(32), .out_width(8), .\type ("zero")) bit_extender_1 (
    .in(multiplexer_1_out), .out(bit_extender_1_out));
  Clock clock_1 (.out(clock_1_out));
  Bit_Extender #(.in_width(32), .out_width(8), .\type ("zero")) bit_extender_2 (
    .in(multiplexer_2_out), .out(bit_extender_2_out));
  Clock clock_2 (.out(clock_2_out));
  Bit_Extender #(.in_width(32), .out_width(24), .\type ("zero")) bit_extender_3 (
    .in(multiplexer_3_out), .out(bit_extender_3_out));
  Clock clock_3 (.out(clock_3_out));
  Register X (.D(bit_extender_1_out), .en(and_1_out), .clk(clock_1_out), .Q(RGBX));  // open: clr
  Register Y (.D(bit_extender_2_out), .en(and_2_out), .clk(clock_2_out), .Q(RGBY));  // open: clr
  Register #(.width(24)) Color (.D(bit_extender_3_out), .en(and_3_out), .clk(clock_3_out), .Q(RGBColor));  // open: clr
endmodule

module TerminalController (
  input  WriteEnableFromBus,
  input  [25:0] AddressFromBus,
  input  [31:0] DataFromBus,
  output WriteToTerminal,
  output [6:0] DataToTerminal
);

  wire comparator_1_eq, comparator_2_eq;

  Comparator #(.width(1)) comparator_1 (.a(1'b1), .b(WriteEnableFromBus), .eq(comparator_1_eq));  // open: gt, lt
  Comparator #(.width(26)) comparator_2 (.a(26'h3ffff00), .b(AddressFromBus), .eq(comparator_2_eq));  // open: gt, lt
  Bit_Extender #(.in_width(32), .out_width(7)) bit_extender_1 (.in(DataFromBus), .out(DataToTerminal));
  and and_1 (WriteToTerminal, comparator_1_eq, comparator_2_eq);
endmodule

module JoystickController (
  input  [31:0] DataFromBus,
  input  WriteEnableFromBus,
  input  [25:0] AddressFromBus,
  input  [3:0] X,
  input  [3:0] Y,
  output WriteEnableToBus,
  output [31:0] DataToBus
);

  wire and_1_out, and_2_out, comparator_1_eq, comparator_2_eq, not_1_out;
  wire [31:0] bit_extender_1_out, bit_extender_2_out;

  assign bit_extender_1_out = {{28{X[3]}}, X};  // Bit_Extender bit_extender_1
  assign bit_extender_2_out = {{28{Y[3]}}, Y};  // Bit_Extender bit_extender_2
  not not_1 (not_1_out, WriteEnableFromBus);
  Comparator #(.width(26)) comparator_1 (.a(AddressFromBus), .b(26'h3ffff50), .eq(comparator_1_eq));  // open: gt, lt
  Comparator #(.width(26)) comparator_2 (.a(AddressFromBus), .b(26'h3ffff54), .eq(comparator_2_eq));  // open: gt, lt
  and and_1 (and_1_out, not_1_out, comparator_1_eq);
  and and_2 (and_2_out, not_1_out, comparator_2_eq);
  Multiplexer #(.width(32)) multiplexer_1 (
    .in0(bit_extender_1_out), .in1(bit_extender_2_out), .out(DataToBus), .sel(and_2_out));
  or or_1 (WriteEnableToBus, and_1_out, and_2_out);

  // Notes on the sheet:
  //   From Bus
  //   From Joystick
  //   X
  //   Y
  //   ToBus
  //   Tristate buffer allowed but not required here.
endmodule

module LEDController (
  input  [25:0] AddressFromBus,
  input  WriteEnable,
  input  [31:0] DataFromBus,
  output LEDState
);

  wire and_1_out, clock_1_out, comparator_1_eq, not_1_out;

  Comparator #(.mode("unsigned"), .width(26)) comparator_1 (
    .a(26'h3ffff4c), .b(AddressFromBus), .eq(comparator_1_eq));  // open: gt, lt
  and and_1 (and_1_out, WriteEnable, comparator_1_eq);
  not not_1 (not_1_out, LEDState);
  Clock clock_1 (.out(clock_1_out));
  Register #(.width(1)) State (.D(not_1_out), .en(and_1_out), .clk(clock_1_out), .Q(LEDState));  // open: clr

  // Notes on the sheet:
  //   LED State
  //   I
endmodule

module SoundControllerSine (
  input  [31:0] DataFromBus,
  input  [25:0] AddressFromBus,
  input  WriteEnableFromBus,
  output [13:0] Frequency,
  output EnableSound,
  output [6:0] Volume
);

  wire and_1_out, and_2_out, and_3_out, clock_1_out, clock_2_out, clock_3_out, comparator_1_eq,
       comparator_2_eq, comparator_3_eq, not_1_out;
  wire [31:0] register_1_q, register_3_q;

  Comparator #(.mode("unsigned"), .width(26)) comparator_1 (
    .a(AddressFromBus), .b(26'h3ffff0c), .eq(comparator_1_eq));  // open: gt, lt
  Comparator #(.mode("unsigned"), .width(26)) comparator_2 (
    .a(AddressFromBus), .b(26'h3ffff08), .eq(comparator_2_eq));  // open: gt, lt
  Comparator #(.mode("unsigned"), .width(26)) comparator_3 (
    .a(AddressFromBus), .b(26'h3ffff04), .eq(comparator_3_eq));  // open: gt, lt
  and and_1 (and_1_out, comparator_1_eq, WriteEnableFromBus);
  and and_2 (and_2_out, comparator_2_eq, WriteEnableFromBus);
  and and_3 (and_3_out, comparator_3_eq, WriteEnableFromBus);
  Clock clock_1 (.out(clock_1_out));
  Clock clock_2 (.out(clock_2_out));
  Register #(.width(32)) register_1 (
    .D(DataFromBus), .en(and_1_out), .clk(clock_1_out), .Q(register_1_q));  // open: clr
  Register #(.width(1)) register_2 (.D(not_1_out), .en(and_2_out), .clk(clock_3_out), .Q(EnableSound));  // open: clr
  Clock clock_3 (.out(clock_3_out));
  Register #(.width(32)) register_3 (
    .D(DataFromBus), .en(and_3_out), .clk(clock_2_out), .Q(register_3_q));  // open: clr
  not not_1 (not_1_out, EnableSound);
  Bit_Extender #(.in_width(32), .out_width(14), .\type ("zero")) bit_extender_1 (.in(register_1_q), .out(Frequency));
  Bit_Extender #(.in_width(32), .out_width(7), .\type ("zero")) bit_extender_2 (.in(register_3_q), .out(Volume));
endmodule

module SoundControllerTriangle (
  input  [31:0] DataFromBus,
  input  [25:0] AddressFromBus,
  input  WriteEnableFromBus,
  output [13:0] Frequency,
  output EnableSound,
  output [6:0] Volume
);

  wire and_1_out, and_2_out, and_3_out, clock_1_out, clock_2_out, clock_3_out, comparator_1_eq,
       comparator_2_eq, comparator_3_eq, not_1_out;
  wire [31:0] register_1_q, register_2_q;

  Comparator #(.mode("unsigned"), .width(26)) comparator_1 (
    .a(AddressFromBus), .b(26'h3ffff18), .eq(comparator_1_eq));  // open: gt, lt
  Comparator #(.mode("unsigned"), .width(26)) comparator_2 (
    .a(AddressFromBus), .b(26'h3ffff1c), .eq(comparator_2_eq));  // open: gt, lt
  Comparator #(.mode("unsigned"), .width(26)) comparator_3 (
    .a(AddressFromBus), .b(26'h3ffff2c), .eq(comparator_3_eq));  // open: gt, lt
  and and_1 (and_1_out, comparator_1_eq, WriteEnableFromBus);
  and and_2 (and_2_out, comparator_2_eq, WriteEnableFromBus);
  and and_3 (and_3_out, comparator_3_eq, WriteEnableFromBus);
  Register #(.width(32)) register_1 (
    .D(DataFromBus), .en(and_1_out), .clk(clock_1_out), .Q(register_1_q));  // open: clr
  Clock clock_1 (.out(clock_1_out));
  Clock clock_2 (.out(clock_2_out));
  Register #(.width(32)) register_2 (
    .D(DataFromBus), .en(and_3_out), .clk(clock_3_out), .Q(register_2_q));  // open: clr
  Clock clock_3 (.out(clock_3_out));
  Register #(.width(1)) register_3 (.D(not_1_out), .en(and_2_out), .clk(clock_2_out), .Q(EnableSound));  // open: clr
  not not_1 (not_1_out, EnableSound);
  Bit_Extender #(.in_width(32), .out_width(14), .\type ("zero")) bit_extender_1 (.in(register_1_q), .out(Frequency));
  Bit_Extender #(.in_width(32), .out_width(7), .\type ("zero")) bit_extender_2 (.in(register_2_q), .out(Volume));
endmodule

module SoundControllerSquare (
  input  [31:0] DataFromBus,
  input  [25:0] AddressFromBus,
  input  WriteEnableFromBus,
  output [13:0] Frequency,
  output EnableSound,
  output [6:0] Volume
);

  wire and_1_out, and_2_out, and_3_out, clock_1_out, clock_2_out, clock_3_out, comparator_1_eq,
       comparator_2_eq, comparator_3_eq, not_1_out;
  wire [31:0] register_1_q, register_2_q;

  Comparator #(.mode("unsigned"), .width(26)) comparator_1 (
    .a(AddressFromBus), .b(26'h3ffff30), .eq(comparator_1_eq));  // open: gt, lt
  Comparator #(.mode("unsigned"), .width(26)) comparator_2 (
    .a(AddressFromBus), .b(26'h3ffff34), .eq(comparator_2_eq));  // open: gt, lt
  Comparator #(.mode("unsigned"), .width(26)) comparator_3 (
    .a(AddressFromBus), .b(26'h3ffff38), .eq(comparator_3_eq));  // open: gt, lt
  and and_1 (and_1_out, comparator_1_eq, WriteEnableFromBus);
  and and_2 (and_2_out, comparator_2_eq, WriteEnableFromBus);
  and and_3 (and_3_out, comparator_3_eq, WriteEnableFromBus);
  Register #(.width(32)) register_1 (
    .D(DataFromBus), .en(and_1_out), .clk(clock_1_out), .Q(register_1_q));  // open: clr
  Clock clock_1 (.out(clock_1_out));
  Clock clock_2 (.out(clock_2_out));
  Register #(.width(32)) register_2 (
    .D(DataFromBus), .en(and_3_out), .clk(clock_3_out), .Q(register_2_q));  // open: clr
  Clock clock_3 (.out(clock_3_out));
  Register #(.width(1)) register_3 (.D(not_1_out), .en(and_2_out), .clk(clock_2_out), .Q(EnableSound));  // open: clr
  not not_1 (not_1_out, EnableSound);
  Bit_Extender #(.in_width(32), .out_width(14), .\type ("zero")) bit_extender_1 (.in(register_1_q), .out(Frequency));
  Bit_Extender #(.in_width(32), .out_width(7), .\type ("zero")) bit_extender_2 (.in(register_2_q), .out(Volume));
endmodule
